// Logisim project LogiSpim.circ as structural Verilog: 20 circuits, main circuit main
module main (
  input  in_1
);

  wire and_4_out, and_5_out, approachingBreakpoint, atBreakpoint_F, CLK, CM_CLK, CM_IsSuspended, CM_TRUE_CLK,
       comparator_1_eq, comparator_2_eq, comparator_3_eq, comparator_3_gt, comparator_4_eq, comparator_4_gt,
       comparator_5_eq, controlpathregister_d_e_1_alusrca_e, controlpathregister_d_e_1_not_aluout_e,
       controlpathregister_d_e_1_writeregsrc_e, controlpathregister_m_w_1_regwrite_w,
       controlunit_1_alusrca_d, controlunit_1_not_aluout_d, controlunit_1_regwrite_d,
       controlunit_1_writeregsrc_d, HazardShieldD_OverrideRegData1, HazardShieldD_OverrideRegData2,
       HazardShieldE_OverrideRegData1, HazardShieldE_OverrideRegData2, InvalidInstructionAddr_F, IsSyscall_F,
       keyboard_1_avail, MM_Data_InvalidAddressFlag, MM_Stack_InvalidAddressFlag, multiplexer_3_out,
       multiplexer_4_out, nextIsSyscall, not_1_out, not_2_out, not_3_out, not_4_out, not_5_out, not_6_out,
       not_7_out, not_8_out, not_9_out, or_3_out, or_4_out, PrintChar_D, PS_Reset, register_1_q, RegWrite_E,
       RegWrite_M, Reset, SkipBreakpoint, SuspendProcessor_D;
  wire [1:0] controlpathregister_d_e_1_alusrcb_e, controlpathregister_m_w_1_regwritedatasrc_w,
       controlunit_1_alusrcb_d, controlunit_1_memtoreg_d, PCSrc_D, RegWriteDataSrc_E, RegWriteDataSrc_M;
  wire [3:0] controlpathregister_d_e_1_memop_e, controlpathregister_e_m_1_memop_m, controlunit_1_memop_d;
  wire [4:0] controlpathregister_d_e_1_alucontrol_e, controlunit_1_alucontrol_d, datapathregister_d_e_1_rd_e,
       datapathregister_d_e_1_rt_e, datapathregister_d_e_1_shamt_e, datapathregister_e_m_1_writereg_m,
       datapathregister_m_w_1_writereg_w, hazardshield_d_1_rs_d, hazardshield_d_1_rt_d,
       MM_Data_MemOpANDAlign, MM_Stack_MemOpANDAlign, multiplexer_10_out, multiplexer_11_out;
  wire [6:0] bit_extender_1_out, keyboard_1_data, MM_Data_Enables, MM_Stack_Enables;
  wire [23:0] MM_Data_RAMAddr, MM_Stack_RAMAddr;
  wire [31:0] a0_D, adder_1_out, adder_2_out, alu_1_q, bit_extender_2_out, bit_extender_3_out,
       datapathregister_d_e_1_pcplus4_e, datapathregister_d_e_1_regdata1_e,
       datapathregister_d_e_1_regdata2_e, datapathregister_d_e_1_signimm_e, datapathregister_e_m_1_aluout_m,
       datapathregister_e_m_1_memwritedata_m, datapathregister_e_m_1_pcplus4_m,
       datapathregister_e_m_1_upperimm_m, datapathregister_f_d_1_instruction_d,
       datapathregister_f_d_1_pcplus4_d, datapathregister_m_w_1_aluout_w,
       datapathregister_m_w_1_memreaddata_w, datapathregister_m_w_1_pcplus4_w,
       datapathregister_m_w_1_upperimm_w, HazardShieldD_RegData1, HazardShieldD_RegData2,
       HazardShieldE_RegData1, HazardShieldE_RegData2, Instruction_F, MM_Data_DataIn, MM_Data_RAMOut,
       mm_postprocessor_1_dataout, MM_Stack_DataIn, multiplexer_1_out, multiplexer_5_out, multiplexer_8_out,
       multiplexer_9_out, multiplexer_12_out, multiplexer_13_out, multiplexer_14_out, multiplexer_15_out,
       multiplexer_16_out, multiplexer_17_out, nextInstruction, nextPC, pc_F, RegData1_D, RegData2_D,
       registerfile_1_registerdata1, registerfile_1_registerdata2, S1_Addr_q, S1_Fetch_q, S2_Addr_q,
       S2_Decode_q, S3_Addr_q, S3_Execute_q, S4_Addr_q, S4_Memory_q, shifter_1_out, shifter_2_out,
       shifter_3_out, stack_section_dout, subtractor_1_out;
  wire [31:30] undriven;

  Bit_Extender #(.in_width(32), .out_width(7), .\type ("zero")) bit_extender_1 (.in(a0_D), .out(bit_extender_1_out));
  Register #(.width(1)) register_1 (.D(PrintChar_D), .clk(CLK), .Q(register_1_q), .clr(Reset));  // open: en
  not not_1 (not_1_out, CLK);
  not not_2 (not_2_out, CLK);
  TTY #(.cols(120), .rows(36)) tty_1 (.data(bit_extender_1_out), .clk(CLK), .we(register_1_q), .clr(Reset));
  Comparator #(.mode("unsigned"), .width(32)) comparator_1 (
    .a(nextPC), .b(32'h400020), .eq(comparator_1_eq));  // open: gt, lt
  Comparator #(.mode("unsigned"), .width(32)) comparator_2 (
    .a(pc_F), .b(32'h400020), .eq(comparator_2_eq));  // open: gt, lt
  Register #(.width(32)) S1_Addr (.D(nextPC), .en(not_3_out), .clk(CLK), .Q(S1_Addr_q), .clr(PS_Reset));
  not not_3 (not_3_out, nextIsSyscall);
  Register #(.width(32)) S1_Fetch (.D(nextInstruction), .en(not_4_out), .clk(CLK), .Q(S1_Fetch_q), .clr(PS_Reset));
  not not_4 (not_4_out, nextIsSyscall);
  Keyboard keyboard_1 (
    .clk(CM_TRUE_CLK), .re(keyboard_1_avail), .avail(keyboard_1_avail), .data(keyboard_1_data));  // open: clr
  KBD_Postprocessor kbd_postprocessor_1 (
    .Data(keyboard_1_data), .CM_TRUE_CLK(CM_TRUE_CLK), .Reset(Reset), .PS_Reset(PS_Reset), .CM_CLK(CM_CLK));
  Multiplexer #(.select(2), .width(32)) multiplexer_1 (
    .in0(adder_1_out), .in1(adder_2_out), .in2(multiplexer_5_out), .in3(32'h80000000),
    .out(multiplexer_1_out), .sel(PCSrc_D));
  InstructionMemory instructionmemory_1 (.Address(nextPC), .Instruction(nextInstruction));  // open: InvalidAddressFlag
  and and_1 (approachingBreakpoint, in_1, comparator_1_eq, not_1_out);
  and and_2 (atBreakpoint_F, in_1, comparator_2_eq, not_2_out);
  Register #(.width(32)) S2_Addr (.D(S1_Addr_q), .en(not_3_out), .clk(CLK), .Q(S2_Addr_q), .clr(PS_Reset));
  Register #(.width(32)) S2_Decode (.D(S1_Fetch_q), .en(not_4_out), .clk(CLK), .Q(S2_Decode_q), .clr(PS_Reset));
  Button button_1 (.out(SkipBreakpoint));
  Register #(.width(32)) S3_Addr (.D(S2_Addr_q), .en(not_3_out), .clk(CLK), .Q(S3_Addr_q), .clr(PS_Reset));
  Register #(.width(32)) S3_Execute (.D(S2_Decode_q), .en(not_4_out), .clk(CLK), .Q(S3_Execute_q), .clr(PS_Reset));
  LED u_atBreakpoint_F (.in(atBreakpoint_F));
  Multiplexer #(.width(32)) multiplexer_2 (.in0(multiplexer_1_out), .in1(32'h400000), .out(nextPC), .sel(Reset));
  or or_1 (IsSyscall_F, comparator_3_gt, comparator_3_eq);
  Comparator #(.mode("unsigned"), .width(32)) comparator_3 (
    .a(pc_F), .b(32'h80000000), .gt(comparator_3_gt), .eq(comparator_3_eq));  // open: lt
  LED u_CLK (.in(CLK));
  Register #(.width(32)) pc (.D(nextPC), .clk(CLK), .Q(pc_F));  // open: en, clr
  Register #(.width(32)) S4_Addr (.D(S3_Addr_q), .en(not_3_out), .clk(CLK), .Q(S4_Addr_q), .clr(PS_Reset));
  Register #(.width(32)) S4_Memory (.D(S3_Execute_q), .en(not_4_out), .clk(CLK), .Q(S4_Memory_q), .clr(PS_Reset));
  or or_2 (nextIsSyscall, comparator_4_gt, comparator_4_eq);
  Comparator #(.mode("unsigned"), .width(32)) comparator_4 (
    .a(nextPC), .b(32'h80000000), .gt(comparator_4_gt), .eq(comparator_4_eq));  // open: lt
  LED u_InvalidInstructionAddr_F (.in(InvalidInstructionAddr_F));
  LED u_CM_IsSuspended (.in(CM_IsSuspended));
  Register #(.width(32)) S5_Addr (.D(S4_Addr_q), .en(not_3_out), .clk(CLK), .clr(PS_Reset));  // open: Q
  Register #(.width(32)) S5_Writeback (.D(S4_Memory_q), .en(not_4_out), .clk(CLK), .clr(PS_Reset));  // open: Q
  Adder #(.width(32)) adder_1 (.a(pc_F), .b(32'h4), .out(adder_1_out));  // open: cin, cout
  InstructionMemory instructionmemory_2 (
    .Address(pc_F), .InvalidAddressFlag(InvalidInstructionAddr_F), .Instruction(Instruction_F));
  Clock clock_1 (.out(CM_TRUE_CLK));
  Multiplexer multiplexer_3 (.in0(CM_CLK), .in1(CM_TRUE_CLK), .out(multiplexer_3_out), .sel(nextIsSyscall));
  DataPathRegister_F_D datapathregister_f_d_1 (
    .Instruction_F(Instruction_F), .PCPlus4_F(adder_1_out), .CLK(CLK), .Reset(Reset),
    .Instruction_D(datapathregister_f_d_1_instruction_d), .PCPlus4_D(datapathregister_f_d_1_pcplus4_d));
  Register #(.width(1)) register_2 (
    .D(or_3_out), .clk(multiplexer_3_out), .Q(CM_IsSuspended), .clr(or_4_out));  // open: en
  or or_3 (or_3_out, CM_IsSuspended, SuspendProcessor_D, InvalidInstructionAddr_F, approachingBreakpoint);
  Multiplexer multiplexer_4 (.in0(1'b0), .in1(SkipBreakpoint), .out(multiplexer_4_out), .sel(in_1));
  // Probe on datapathregister_f_d_1_instruction_d[31:26]
  // Probe on datapathregister_f_d_1_instruction_d[5:0]
  // Probe on datapathregister_f_d_1_instruction_d[25:21]
  // Probe on datapathregister_f_d_1_instruction_d[20:16]
  // Probe on datapathregister_f_d_1_instruction_d[15:11]
  // Probe on datapathregister_f_d_1_instruction_d[15:0]
  or or_4 (or_4_out, Reset, multiplexer_4_out);
  and and_3 (CLK, multiplexer_3_out, ~CM_IsSuspended);  // AND_Gate
  Subtractor #(.width(32)) subtractor_1 (
    .a(datapathregister_f_d_1_pcplus4_d), .b(32'h4), .out(subtractor_1_out));  // open: bin, bout
  // Probe on controlpathregister_m_w_1_regwrite_w
  Comparator #(.width(6)) comparator_5 (
    .a(datapathregister_f_d_1_instruction_d[31:26]), .b({6{1'b0}}), .eq(comparator_5_eq));  // open: gt, lt
  Shifter #(.width(32)) shifter_1 (
    .in({undriven, subtractor_1_out[31:28], datapathregister_f_d_1_instruction_d[25:0]}), .\dist (5'b00010),
    .out(shifter_1_out));
  // Probe on multiplexer_5_out
  Multiplexer #(.width(32)) multiplexer_5 (
    .in0(shifter_1_out), .in1(RegData1_D), .out(multiplexer_5_out), .sel(comparator_5_eq));
  RegisterFile registerfile_1 (
    .Address1(datapathregister_f_d_1_instruction_d[25:21]),
    .Address2(datapathregister_f_d_1_instruction_d[20:16]),
    .WriteEnable3(controlpathregister_m_w_1_regwrite_w), .Address3(datapathregister_m_w_1_writereg_w),
    .WriteData3(multiplexer_17_out), .CLK(CLK), .Reset(Reset), .RegisterData1(registerfile_1_registerdata1),
    .RegisterData2(registerfile_1_registerdata2), .a0(a0_D));
  assign bit_extender_2_out = {{16{datapathregister_f_d_1_instruction_d[15]}}, datapathregister_f_d_1_instruction_d[15:0]};  // Bit_Extender bit_extender_2
  HazardShield_D hazardshield_d_1 (
    .Instruction_D(datapathregister_f_d_1_instruction_d), .RegWrite_E(RegWrite_E), .IsMemOp_E(and_5_out),
    .WriteReg_E(multiplexer_11_out), .RegWriteData_E(multiplexer_14_out), .RegWrite_M(RegWrite_M),
    .WriteReg_M(datapathregister_e_m_1_writereg_m), .RegWriteData_M(multiplexer_16_out),
    .rs_D(hazardshield_d_1_rs_d), .rt_D(hazardshield_d_1_rt_d),
    .OverrideRegData1_D(HazardShieldD_OverrideRegData1), .RegData1_D(HazardShieldD_RegData1),
    .OverrideRegData2_D(HazardShieldD_OverrideRegData2), .RegData2_D(HazardShieldD_RegData2));
  not not_5 (not_5_out, HazardShieldD_OverrideRegData1);
  Multiplexer #(.width(32)) multiplexer_6 (
    .in0(HazardShieldD_RegData1), .in1(registerfile_1_registerdata1), .out(RegData1_D), .sel(not_5_out));
  Shifter #(.width(32)) shifter_2 (.in(bit_extender_2_out), .\dist (5'b00010), .out(shifter_2_out));
  Adder #(.width(32)) adder_2 (
    .a(datapathregister_f_d_1_pcplus4_d), .b(shifter_2_out), .out(adder_2_out));  // open: cin, cout
  // Probe on adder_2_out
  ControlUnit controlunit_1 (
    .Op(datapathregister_f_d_1_instruction_d[31:26]), .Funct(datapathregister_f_d_1_instruction_d[5:0]),
    .RegData1_D(RegData1_D), .RegData2_D(RegData2_D), .RegWrite_D(controlunit_1_regwrite_d),
    .MemToReg_D(controlunit_1_memtoreg_d), .MemOp_D(controlunit_1_memop_d),
    .ALUControl_D(controlunit_1_alucontrol_d), .NOT_ALUOut_D(controlunit_1_not_aluout_d),
    .ALUSrcA_D(controlunit_1_alusrca_d), .ALUSrcB_D(controlunit_1_alusrcb_d),
    .WriteRegSrc_D(controlunit_1_writeregsrc_d), .PCSrc_D(PCSrc_D), .SuspendProcessor_D(PrintChar_D),
    .PrintChar_D(SuspendProcessor_D));
  not not_6 (not_6_out, HazardShieldD_OverrideRegData2);
  Multiplexer #(.width(32)) multiplexer_7 (
    .in0(HazardShieldD_RegData2), .in1(registerfile_1_registerdata2), .out(RegData2_D), .sel(not_6_out));
  ControlPathRegister_D_E controlpathregister_d_e_1 (
    .RegWrite_D(controlunit_1_regwrite_d), .RegWriteDataSrc_D(controlunit_1_memtoreg_d),
    .MemOp_D(controlunit_1_memop_d), .ALUControl_D(controlunit_1_alucontrol_d),
    .NOT_ALUOut_D(controlunit_1_not_aluout_d), .ALUSrcA_D(controlunit_1_alusrca_d),
    .ALUSrcB_D(controlunit_1_alusrcb_d), .WriteRegSrc_D(controlunit_1_writeregsrc_d), .CLK(CLK),
    .Reset(Reset), .RegWrite_E(RegWrite_E), .RegWriteDataSrc_E(RegWriteDataSrc_E),
    .MemOp_E(controlpathregister_d_e_1_memop_e), .ALUControl_E(controlpathregister_d_e_1_alucontrol_e),
    .NOT_ALUOut_E(controlpathregister_d_e_1_not_aluout_e), .ALUSrcA_E(controlpathregister_d_e_1_alusrca_e),
    .ALUSrcB_E(controlpathregister_d_e_1_alusrcb_e), .WriteRegSrc_E(controlpathregister_d_e_1_writeregsrc_e));
  DataPathRegister_D_E datapathregister_d_e_1 (
    .RegData1_D(RegData1_D), .RegData2_D(RegData2_D), .rt_D(datapathregister_f_d_1_instruction_d[20:16]),
    .rd_D(datapathregister_f_d_1_instruction_d[15:11]), .shamt_D(datapathregister_f_d_1_instruction_d[10:6]),
    .SignImm_D(bit_extender_2_out), .PCPlus4_D(datapathregister_f_d_1_pcplus4_d), .CLK(CLK), .Reset(Reset),
    .RegData1_E(datapathregister_d_e_1_regdata1_e), .RegData2_E(datapathregister_d_e_1_regdata2_e),
    .rt_E(datapathregister_d_e_1_rt_e), .rd_E(datapathregister_d_e_1_rd_e),
    .shamt_E(datapathregister_d_e_1_shamt_e), .SignImm_E(datapathregister_d_e_1_signimm_e),
    .PCPlus4_E(datapathregister_d_e_1_pcplus4_e));
  HazardShield_E hazardshield_e_1 (
    .rs_D(hazardshield_d_1_rs_d), .rt_D(hazardshield_d_1_rt_d), .RegWrite_M(RegWrite_M),
    .WriteReg_M(datapathregister_e_m_1_writereg_m), .RegWriteData_M(multiplexer_16_out), .CLK(CLK),
    .Reset(Reset), .OverrideRegData1_E(HazardShieldE_OverrideRegData1), .RegData1_E(HazardShieldE_RegData1),
    .OverrideRegData2_E(HazardShieldE_OverrideRegData2), .RegData2_E(HazardShieldE_RegData2));
  not not_7 (not_7_out, HazardShieldE_OverrideRegData1);
  Multiplexer #(.width(32)) multiplexer_8 (
    .in0(HazardShieldE_RegData1), .in1(datapathregister_d_e_1_regdata1_e), .out(multiplexer_8_out),
    .sel(not_7_out));
  assign bit_extender_3_out = {{27{1'b0}}, datapathregister_d_e_1_shamt_e};  // Bit_Extender bit_extender_3
  not not_8 (not_8_out, HazardShieldE_OverrideRegData2);
  Multiplexer #(.width(32)) multiplexer_9 (
    .in0(HazardShieldE_RegData2), .in1(datapathregister_d_e_1_regdata2_e), .out(multiplexer_9_out),
    .sel(not_8_out));
  // Probe on controlpathregister_d_e_1_writeregsrc_e
  Multiplexer #(.width(5)) multiplexer_10 (
    .in0(datapathregister_d_e_1_rt_e), .in1(datapathregister_d_e_1_rd_e), .out(multiplexer_10_out),
    .sel(controlpathregister_d_e_1_writeregsrc_e));
  and and_4 (and_4_out, RegWriteDataSrc_E[0], RegWriteDataSrc_E[1]);
  Multiplexer #(.width(5)) multiplexer_11 (
    .in0(multiplexer_10_out), .in1({5{1'b1}}), .out(multiplexer_11_out), .sel(and_4_out));
  // Probe on controlpathregister_d_e_1_alusrcb_e
  Shifter #(.width(32)) shifter_3 (.in(datapathregister_d_e_1_signimm_e), .\dist (5'b10000), .out(shifter_3_out));
  // Probe on controlpathregister_d_e_1_alusrca_e
  Multiplexer #(.select(2), .width(32)) multiplexer_12 (
    .in0(multiplexer_9_out), .in1(datapathregister_d_e_1_signimm_e),
    .in2({{16{1'b0}}, datapathregister_d_e_1_signimm_e[15:0]}), .in3(datapathregister_d_e_1_signimm_e),
    .out(multiplexer_12_out), .sel(controlpathregister_d_e_1_alusrcb_e));
  Multiplexer #(.width(32)) multiplexer_13 (
    .in0(multiplexer_8_out), .in1(bit_extender_3_out), .out(multiplexer_13_out),
    .sel(controlpathregister_d_e_1_alusrca_e));
  // Probe on controlpathregister_d_e_1_not_aluout_e
  // Probe on controlpathregister_d_e_1_alucontrol_e
  ALU alu_1 (
    .ALUControl(controlpathregister_d_e_1_alucontrol_e), .A(multiplexer_13_out), .B(multiplexer_12_out),
    .NOT_ALUOutput(controlpathregister_d_e_1_not_aluout_e), .CLK(CLK), .Reset(Reset), .Q(alu_1_q));
  // Probe on alu_1_q
  // Probe on shifter_3_out
  // Probe on multiplexer_9_out
  // Probe on multiplexer_11_out
  // Probe on datapathregister_d_e_1_pcplus4_e
  and and_5 (and_5_out, ~RegWriteDataSrc_E[1], RegWriteDataSrc_E[0]);  // AND_Gate
  Multiplexer #(.select(2), .width(32)) multiplexer_14 (
    .in0(alu_1_q), .in2(shifter_3_out), .in3(datapathregister_d_e_1_pcplus4_e), .out(multiplexer_14_out),
    .sel(RegWriteDataSrc_E));  // open: in1
  ControlPathRegister_E_M controlpathregister_e_m_1 (
    .RegWrite_E(RegWrite_E), .RegWriteDataSrc_E(RegWriteDataSrc_E),
    .MemOp_E(controlpathregister_d_e_1_memop_e), .CLK(CLK), .Reset(Reset), .RegWrite_M(RegWrite_M),
    .RegWriteDataSrc_M(RegWriteDataSrc_M), .MemOp_M(controlpathregister_e_m_1_memop_m));
  DataPathRegister_E_M datapathregister_e_m_1 (
    .ALUOut_E(alu_1_q), .UpperImm_E(shifter_3_out), .MemWriteData_E(multiplexer_9_out),
    .WriteReg_E(multiplexer_11_out), .PCPlus4_E(datapathregister_d_e_1_pcplus4_e), .CLK(CLK), .Reset(Reset),
    .ALUOut_M(datapathregister_e_m_1_aluout_m), .UpperImm_M(datapathregister_e_m_1_upperimm_m),
    .MemWriteData_M(datapathregister_e_m_1_memwritedata_m), .WriteReg_M(datapathregister_e_m_1_writereg_m),
    .PCPlus4_M(datapathregister_e_m_1_pcplus4_m));
  // Probe on controlpathregister_e_m_1_memop_m
  not not_9 (not_9_out, CM_IsSuspended);
  Multiplexer #(.width(32)) multiplexer_15 (
    .in0(32'hfffffffc), .in1(datapathregister_e_m_1_aluout_m), .out(multiplexer_15_out), .sel(not_9_out));
  MM_Preprocessor mm_preprocessor_1 (
    .MemOp(controlpathregister_e_m_1_memop_m), .Address(multiplexer_15_out),
    .InputData(datapathregister_e_m_1_memwritedata_m), .CLK(CLK), .Data_MemOpANDAlign(MM_Data_MemOpANDAlign),
    .Data_RAMAddr(MM_Data_RAMAddr), .Data_Enables(MM_Data_Enables), .Data_DataIn(MM_Data_DataIn),
    .Data_InvalidAddressFlag(MM_Data_InvalidAddressFlag), .Stack_MemOpANDAlign(MM_Stack_MemOpANDAlign),
    .Stack_RAMAddr(MM_Stack_RAMAddr), .Stack_Enables(MM_Stack_Enables), .Stack_DataIn(MM_Stack_DataIn),
    .Stack_InvalidAddressFlag(MM_Stack_InvalidAddressFlag));
  RAM #(.addrWidth(24), .asyncread("true"), .byteenables("byteEnables"), .dataWidth(32), .trigger("falling"), .\type ("nonvolatile")) data_section (
    .addr(MM_Data_RAMAddr), .we(MM_Data_Enables[0]), .oe(MM_Data_Enables[1]), .clk(MM_Data_Enables[6]),
    .din(MM_Data_DataIn), .dout(MM_Data_RAMOut), .be3(MM_Data_Enables[2]), .be2(MM_Data_Enables[3]),
    .be1(MM_Data_Enables[4]), .be0(MM_Data_Enables[5]));
  RAM #(.addrWidth(24), .asyncread("true"), .byteenables("byteEnables"), .dataWidth(32), .trigger("falling"), .\type ("nonvolatile")) stack_section (
    .addr(MM_Stack_RAMAddr), .we(MM_Stack_Enables[0]), .oe(MM_Stack_Enables[1]), .clk(MM_Stack_Enables[6]),
    .din(MM_Stack_DataIn), .dout(stack_section_dout), .be3(MM_Stack_Enables[2]), .be2(MM_Stack_Enables[3]),
    .be1(MM_Stack_Enables[4]), .be0(MM_Stack_Enables[5]));
  MM_Postprocessor mm_postprocessor_1 (
    .Data_MemOpANDAlignment(MM_Data_MemOpANDAlign), .Data_RAMOut(MM_Data_RAMOut),
    .Data_InvalidAddressFlag(MM_Data_InvalidAddressFlag), .Stack_MemOpANDAlignment(MM_Stack_MemOpANDAlign),
    .Stack_RAMOut(stack_section_dout), .Stack_InvalidAddressFlag(MM_Stack_InvalidAddressFlag),
    .DataOut(mm_postprocessor_1_dataout));  // open: AdES_AddressErrorException
  Multiplexer #(.select(2), .width(32)) multiplexer_16 (
    .in0(datapathregister_e_m_1_aluout_m), .in1(mm_postprocessor_1_dataout),
    .in2(datapathregister_e_m_1_upperimm_m), .in3(datapathregister_e_m_1_pcplus4_m),
    .out(multiplexer_16_out), .sel(RegWriteDataSrc_M));
  // Probe on mm_postprocessor_1_dataout
  // Probe on datapathregister_e_m_1_upperimm_m
  // Probe on datapathregister_e_m_1_aluout_m
  // Probe on datapathregister_e_m_1_writereg_m
  // Probe on datapathregister_e_m_1_pcplus4_m
  ControlPathRegister_M_W controlpathregister_m_w_1 (
    .RegWrite_M(RegWrite_M), .RegWriteDataSrc_M(RegWriteDataSrc_M), .CLK(CLK), .Reset(Reset),
    .RegWrite_W(controlpathregister_m_w_1_regwrite_w),
    .RegWriteDataSrc_W(controlpathregister_m_w_1_regwritedatasrc_w));
  DataPathRegister_M_W datapathregister_m_w_1 (
    .ALUOut_M(datapathregister_e_m_1_aluout_m), .UpperImm_M(datapathregister_e_m_1_upperimm_m),
    .MemReadData_M(mm_postprocessor_1_dataout), .PCPlus4_M(datapathregister_e_m_1_pcplus4_m),
    .WriteReg_M(datapathregister_e_m_1_writereg_m), .CLK(CLK), .Reset(Reset),
    .ALUOut_W(datapathregister_m_w_1_aluout_w), .UpperImm_W(datapathregister_m_w_1_upperimm_w),
    .MemReadData_W(datapathregister_m_w_1_memreaddata_w), .PCPlus4_W(datapathregister_m_w_1_pcplus4_w),
    .WriteReg_W(datapathregister_m_w_1_writereg_w));
  // Probe on datapathregister_m_w_1_writereg_w
  // Probe on controlpathregister_m_w_1_regwritedatasrc_w
  Multiplexer #(.select(2), .width(32)) multiplexer_17 (
    .in0(datapathregister_m_w_1_aluout_w), .in1(datapathregister_m_w_1_memreaddata_w),
    .in2(datapathregister_m_w_1_upperimm_w), .in3(datapathregister_m_w_1_pcplus4_w),
    .out(multiplexer_17_out), .sel(controlpathregister_m_w_1_regwritedatasrc_w));
  // Probe on multiplexer_17_out

  // Other names for the same wires on the sheet: EnableBreakpoint = in_1

  // Notes on the sheet:
  //   PCSrc_D
  //   00 - PCPlus4_F
  //   01 - PCBranchAddr_D
  //   10 - PCJumpAddr_D
  //   11 - Syscall Start Addr
  //   Keyboard Guide:
  //   Breakpoint Logic
  //   Keyboard
  //   Select the box under "Keyboard" with the poke (hand) tool.
  //   While selected (and a high auto-tick frequency is set), the
  //   keyboard allows for the following operations based on the
  //   presses of the following keys:
  //   r = Reset Processor
  //   [Space] = Cycle Clock
  //   t = Toggle Auto-Ticking
  //   **Note: Registers in the RegisterFile are
  //   returns to LOW.
  //   written to on FALLING edges of the clock.
  //   Therefore, the instruction in S5 will not have
  //   register writeback shown until the clock
  //   User Control Assistance Circuitry
  //   Reset
  //   0 - No Change
  //   1 - PC Reset Value
  //   PC Reset Value
  //   Used for the control panel in the top left
  //   Pipeline State
  //   Breakpoints
  //   Emulated Console
  //   Determines if the next instruction will be executing a syscall.
  //   (used by Clock Management unit for user experience)
  //   Status Indicators
  //   (likely due to invalid jump/branch)
  //   a set of signals are HIGH.
  //   op [31:26]
  //   Clock Management (CM)
  //   This unit allows for syscalls to be essentially masked from user
  //   view by auto-ticking the clock during execution of kernel code.
  //   Additionally, there is functionality to suspend CLK when any of
  //   funct [5:0]
  //   addr [25:0]
  //   op [31:26]
  //   <- Clock
  //   rt [20:16]
  //   Suspension
  //   Circuitry
  //   rs [25:21]
  //   rt [20:16]
  //   rd [15:11]
  //   shamt [10:6]
  //   imm [15:0]
  //   Computing JTA
  //   (Jump Target Address)
  //   PCJumpAddr is set to rs value if
  //   is R-Type Instruction (jr/jalr)
  //   Data Forwarding
  //   Computing BTA
  //   (Branch Target Address)
  //   Reverse-Direction Control Path
  //   Data Forwarding
  //   (If RegWriteDataSrc_E == 0b11, WriteReg_E is $ra)
  //   (Done for debugging to display stack) ->
  //   LOAD "data.hex" FILE HERE!
  //   RIGHT CLICK RAM:
  //   Load Image > Choose "data.hex"
  //   =======>>
  //   =======>>
  //   Main Memory (MM)
endmodule

module ControlUnit (
  input  [5:0] Op,
  input  [5:0] Funct,
  input  [31:0] RegData1_D,
  input  [31:0] RegData2_D,
  output RegWrite_D,
  output [1:0] MemToReg_D,
  output [3:0] MemOp_D,
  output [4:0] ALUControl_D,
  output NOT_ALUOut_D,
  output ALUSrcA_D,
  output [1:0] ALUSrcB_D,
  output WriteRegSrc_D,
  output [1:0] PCSrc_D,
  output SuspendProcessor_D,
  output PrintChar_D
);

  wire and_2_out, and_3_out, comparator_3_eq, comparator_4_eq, comparator_5_eq, comparator_6_eq,
       comparator_6_lt, decoder_1_out1, decoder_1_out3, multiplexer_1_out, multiplexer_2_out, not_1_out,
       not_2_out, or_1_out;
  wire [1:0] maindecoder_1_branchop;
  wire [3:0] maindecoder_1_aluop;
  wire [3:1] or_2_out;

  // Probe on maindecoder_1_branchop
  Decoder #(.enable("false"), .select(2)) decoder_1 (
    .out1(decoder_1_out1), .out2(or_2_out[2]), .out3(decoder_1_out3), .sel(maindecoder_1_branchop));  // open: out0
  Comparator #(.width(6)) comparator_1 (.a(Op), .b(6'b010100), .eq(SuspendProcessor_D));  // open: gt, lt
  Comparator #(.width(6)) comparator_2 (.a(Op), .b(6'b010101), .eq(PrintChar_D));  // open: gt, lt
  Comparator #(.width(6)) comparator_3 (.a(Op), .b({6{1'b0}}), .eq(comparator_3_eq));  // open: gt, lt
  Comparator #(.width(6)) comparator_4 (.a(Funct), .b(6'b001100), .eq(comparator_4_eq));  // open: gt, lt
  MainDecoder maindecoder_1 (
    .Op(Op), .Funct(Funct), .RegWrite(RegWrite_D), .RegWriteDataSrc(MemToReg_D), .MemOp(MemOp_D),
    .BranchOp(maindecoder_1_branchop), .ALUOp(maindecoder_1_aluop), .ALUSrcA(ALUSrcA_D), .ALUSrcB(ALUSrcB_D),
    .WriteRegSrc(WriteRegSrc_D));
  ALUDecoder aludecoder_1 (
    .ALUOp(maindecoder_1_aluop), .Funct(Funct), .NOT_ALUOut(NOT_ALUOut_D), .ALUControl(ALUControl_D));
  Comparator #(.width(32)) comparator_5 (.a(RegData1_D), .b(RegData2_D), .eq(comparator_5_eq));  // open: gt, lt
  Comparator #(.width(32)) comparator_6 (
    .a(RegData1_D), .b({32{1'b0}}), .eq(comparator_6_eq), .lt(comparator_6_lt));  // open: gt
  or or_1 (or_1_out, comparator_6_eq, comparator_6_lt);
  and and_1 (or_2_out[3], comparator_3_eq, comparator_4_eq);
  Multiplexer multiplexer_1 (.in0(comparator_5_eq), .in1(not_1_out), .out(multiplexer_1_out), .sel(Op[0]));
  not not_1 (not_1_out, comparator_5_eq);
  Multiplexer multiplexer_2 (.in0(or_1_out), .in1(not_2_out), .out(multiplexer_2_out), .sel(Op[0]));
  not not_2 (not_2_out, or_1_out);
  and and_2 (and_2_out, decoder_1_out1, multiplexer_1_out);
  and and_3 (and_3_out, decoder_1_out3, multiplexer_2_out);
  or or_2 (or_2_out[1], and_2_out, and_3_out);
  BitFinder #(.\type ("high1"), .width(4)) bitfinder_1 (.in({or_2_out, 1'b1}), .index(PCSrc_D));  // open: found

  // Other names for the same wires on the sheet: PCSrc[1:0] = PCSrc_D

  // Notes on the sheet:
  //   OP [0]
  //   If OP = 20 (0x14), is exit instruction
  //   If OP = 21 (0x15), is print char instruction
  //   Jump Instruction
  //   R-Type w/Func = 0xc is syscall
  //   Used to negate branch-ability for beq/blez if is bne/bgtz
  //   <--
  //   Jump/Branching Logic
  //   <-- Defaults PCSrc_D to 0b00
  //   <-- Branch if conditional branch is indicated
  //   <-- If is jump instruction, PCSrc_D == 0b10
  //   <-- If is syscall instruction, PCSrc_D == 0b11
  //   This acts similar to the reverse of a decoder. It
  //   <-- outputs the bit address of the highest bit that is a 1.
  //   and condition is satisfied, hence PCSrc_D == 0b01
endmodule

module MainDecoder (
  input  [5:0] Op,
  input  [5:0] Funct,
  output RegWrite,
  output [1:0] RegWriteDataSrc,
  output [3:0] MemOp,
  output [1:0] BranchOp,
  output [3:0] ALUOp,
  output ALUSrcA,
  output [1:0] ALUSrcB,
  output WriteRegSrc
);

  wire and_1_out, and_2_out, and_3_out, and_4_out, and_5_out, and_6_out, and_7_out, and_8_out, and_9_out,
       and_10_out, and_11_out, and_12_out, and_13_out, and_14_out, and_15_out, and_16_out, and_17_out,
       and_18_out, and_19_out, and_20_out, and_21_out, and_22_out, and_23_out, and_24_out, and_25_out,
       and_26_out, and_27_out, and_28_out, and_29_out, and_30_out, and_31_out, and_32_out, and_33_out,
       and_34_out, and_35_out, and_36_out, and_37_out, and_38_out, and_39_out, and_40_out, and_41_out,
       and_42_out, and_43_out, and_44_out, and_45_out, and_46_out, and_47_out, and_48_out, and_49_out,
       and_50_out, and_51_out, and_52_out, and_53_out, and_54_out, and_55_out, and_56_out, and_57_out,
       and_58_out, and_59_out, and_60_out, and_61_out, and_62_out, and_63_out, and_64_out, and_65_out,
       and_66_out, and_67_out, and_68_out, and_69_out, and_70_out, and_71_out, and_72_out, and_73_out,
       or_1_out, or_2_out, or_3_out, or_4_out, undriven;
  wire [63:0] and_74_out, and_75_out, and_76_out, and_77_out, and_78_out, and_79_out, and_80_out, and_81_out,
       and_82_out, and_83_out, and_84_out, and_85_out, and_86_out, and_87_out, and_88_out, and_89_out,
       and_90_out, and_91_out, and_92_out, and_93_out, and_94_out, and_95_out, and_96_out, and_97_out,
       and_98_out, and_99_out, and_100_out, and_101_out, and_102_out, and_103_out, and_104_out, and_105_out,
       and_106_out, and_107_out, and_108_out, and_109_out, and_110_out, and_111_out, and_112_out,
       and_113_out, and_114_out, and_115_out, and_116_out, and_117_out, and_118_out, and_119_out,
       and_120_out, and_121_out, and_122_out, and_123_out, and_124_out, and_125_out, and_126_out,
       and_127_out, and_128_out, and_129_out, and_130_out, and_131_out, and_132_out, and_133_out,
       and_134_out, and_135_out, and_136_out, and_137_out, and_138_out, and_139_out, and_140_out,
       and_141_out, bit_extender_1_out, bit_extender_2_out, bit_extender_3_out, bit_extender_4_out,
       bit_extender_5_out, bit_extender_6_out, bit_extender_7_out, bit_extender_8_out, bit_extender_9_out,
       bit_extender_10_out, bit_extender_11_out, bit_extender_12_out, bit_extender_13_out,
       bit_extender_14_out, bit_extender_15_out, bit_extender_16_out, bit_extender_17_out,
       bit_extender_18_out, bit_extender_19_out, bit_extender_20_out, bit_extender_21_out,
       bit_extender_22_out, bit_extender_23_out, bit_extender_24_out, bit_extender_25_out,
       bit_extender_26_out, bit_extender_27_out, bit_extender_28_out, bit_extender_29_out,
       bit_extender_30_out, bit_extender_31_out, bit_extender_32_out, bit_extender_33_out,
       bit_extender_34_out, bit_extender_35_out, bit_extender_36_out, bit_extender_37_out,
       bit_extender_38_out, bit_extender_39_out, bit_extender_40_out, bit_extender_41_out,
       bit_extender_42_out, bit_extender_43_out, bit_extender_44_out, bit_extender_45_out,
       bit_extender_46_out, bit_extender_47_out, bit_extender_48_out, bit_extender_49_out,
       bit_extender_50_out, bit_extender_51_out, bit_extender_52_out, bit_extender_53_out,
       bit_extender_54_out, bit_extender_55_out, bit_extender_56_out, bit_extender_57_out,
       bit_extender_58_out, bit_extender_59_out, bit_extender_60_out, bit_extender_61_out,
       bit_extender_62_out, bit_extender_63_out, bit_extender_64_out, bit_extender_65_out,
       bit_extender_66_out, bit_extender_67_out, bit_extender_68_out, or_6_out, or_7_out, or_8_out, or_9_out,
       or_10_out, or_11_out, or_12_out, or_13_out, or_14_out, or_15_out, or_16_out, or_17_out, or_18_out,
       or_19_out, or_20_out, or_21_out, or_22_out, or_23_out, or_24_out, or_25_out, or_26_out, or_27_out,
       or_28_out, or_29_out, or_30_out, or_31_out, or_32_out, or_33_out, or_34_out, or_35_out, or_36_out,
       or_37_out, or_38_out, or_39_out, or_40_out, or_41_out, or_42_out, or_43_out, or_44_out, or_45_out,
       or_46_out, or_47_out, or_48_out, or_49_out, or_50_out, or_51_out, or_52_out, or_53_out, or_54_out,
       or_55_out, or_56_out, or_57_out, or_58_out, or_59_out, or_60_out, or_61_out, or_62_out, or_63_out,
       or_64_out, or_65_out, or_66_out, or_67_out, or_68_out, or_69_out, or_70_out, or_71_out, or_72_out;
  wire [63:17] or_5_out;

  and and_1 (and_1_out, ~Op[5], ~Op[4], ~Op[3], ~Op[2], ~Op[1], ~Op[0]);  // AND_Gate
  or or_1 (or_1_out, and_2_out, or_2_out);
  and and_2 (and_2_out, ~Funct[5], ~Funct[4], Funct[3], ~Funct[2], ~Funct[1], ~Funct[0]);  // AND_Gate
  or or_2 (or_2_out, and_3_out, or_3_out);
  and and_3 (and_3_out, ~Funct[5], ~Funct[4], Funct[3], ~Funct[2], ~Funct[1], Funct[0]);  // AND_Gate
  or or_3 (or_3_out, and_4_out, or_4_out);
  and and_4 (and_4_out, ~Funct[5], ~Funct[4], Funct[3], Funct[2], ~Funct[1], ~Funct[0]);  // AND_Gate
  or or_4 (or_4_out, and_5_out, and_5_out);
  and and_5 (and_5_out, ~Funct[5], ~Funct[4], ~Funct[3], ~Funct[2]);  // AND_Gate
  and and_6 (and_6_out, ~Op[5], ~Op[4], ~Op[3], ~Op[2], ~Op[1], Op[0]);  // AND_Gate
  and and_7 (and_7_out, ~Op[5], ~Op[4], ~Op[3], ~Op[2], Op[1], ~Op[0]);  // AND_Gate
  and and_8 (and_8_out, ~Op[5], ~Op[4], ~Op[3], ~Op[2], Op[1], Op[0]);  // AND_Gate
  and and_9 (and_9_out, ~Op[5], ~Op[4], ~Op[3], Op[2], ~Op[1], ~Op[0]);  // AND_Gate
  and and_10 (and_10_out, ~Op[5], ~Op[4], ~Op[3], Op[2], ~Op[1], Op[0]);  // AND_Gate
  and and_11 (and_11_out, ~Op[5], ~Op[4], ~Op[3], Op[2], Op[1], ~Op[0]);  // AND_Gate
  and and_12 (and_12_out, ~Op[5], ~Op[4], ~Op[3], Op[2], Op[1], Op[0]);  // AND_Gate
  and and_13 (and_13_out, ~Op[5], ~Op[4], Op[3], ~Op[2], ~Op[1], ~Op[0]);  // AND_Gate
  and and_14 (and_14_out, ~Op[5], ~Op[4], Op[3], ~Op[2], ~Op[1], Op[0]);  // AND_Gate
  and and_15 (and_15_out, ~Op[5], ~Op[4], Op[3], ~Op[2], Op[1], ~Op[0]);  // AND_Gate
  and and_16 (and_16_out, ~Op[5], ~Op[4], Op[3], ~Op[2], Op[1], Op[0]);  // AND_Gate
  and and_17 (and_17_out, ~Op[5], ~Op[4], Op[3], Op[2], ~Op[1], ~Op[0]);  // AND_Gate
  and and_18 (and_18_out, ~Op[5], ~Op[4], Op[3], Op[2], ~Op[1], Op[0]);  // AND_Gate
  and and_19 (and_19_out, ~Op[5], ~Op[4], Op[3], Op[2], Op[1], ~Op[0]);  // AND_Gate
  and and_20 (and_20_out, ~Op[5], ~Op[4], Op[3], Op[2], Op[1], Op[0]);  // AND_Gate
  and and_21 (and_21_out, ~Op[5], Op[4], ~Op[3], ~Op[2], ~Op[1], ~Op[0]);  // AND_Gate
  and and_22 (and_22_out, ~Op[5], Op[4], ~Op[3], ~Op[2], ~Op[1], Op[0]);  // AND_Gate
  and and_23 (and_23_out, ~Op[5], Op[4], ~Op[3], ~Op[2], Op[1], ~Op[0]);  // AND_Gate
  and and_24 (and_24_out, ~Op[5], Op[4], ~Op[3], ~Op[2], Op[1], Op[0]);  // AND_Gate
  and and_25 (and_25_out, ~Op[5], Op[4], ~Op[3], Op[2], ~Op[1], ~Op[0]);  // AND_Gate
  and and_26 (and_26_out, ~Op[5], Op[4], ~Op[3], Op[2], ~Op[1], Op[0]);  // AND_Gate
  and and_27 (and_27_out, ~Op[5], Op[4], ~Op[3], Op[2], Op[1], ~Op[0]);  // AND_Gate
  and and_28 (and_28_out, ~Op[5], Op[4], ~Op[3], Op[2], Op[1], Op[0]);  // AND_Gate
  and and_29 (and_29_out, ~Op[5], Op[4], Op[3], ~Op[2], ~Op[1], ~Op[0]);  // AND_Gate
  and and_30 (and_30_out, ~Op[5], Op[4], Op[3], ~Op[2], ~Op[1], Op[0]);  // AND_Gate
  and and_31 (and_31_out, ~Op[5], Op[4], Op[3], ~Op[2], Op[1], ~Op[0]);  // AND_Gate
  and and_32 (and_32_out, ~Op[5], Op[4], Op[3], ~Op[2], Op[1], Op[0]);  // AND_Gate
  and and_33 (and_33_out, ~Op[5], Op[4], Op[3], Op[2], ~Op[1], ~Op[0]);  // AND_Gate
  and and_34 (and_34_out, ~Op[5], Op[4], Op[3], Op[2], ~Op[1], Op[0]);  // AND_Gate
  and and_35 (and_35_out, ~Op[5], Op[4], Op[3], Op[2], Op[1], ~Op[0]);  // AND_Gate
  and and_36 (and_36_out, ~Op[5], Op[4], Op[3], Op[2], Op[1], Op[0]);  // AND_Gate
  and and_37 (and_37_out, Op[5], ~Op[4], ~Op[3], ~Op[2], ~Op[1], ~Op[0]);  // AND_Gate
  and and_38 (and_38_out, Op[5], ~Op[4], ~Op[3], ~Op[2], ~Op[1], Op[0]);  // AND_Gate
  and and_39 (and_39_out, Op[5], ~Op[4], ~Op[3], ~Op[2], Op[1], ~Op[0]);  // AND_Gate
  and and_40 (and_40_out, Op[5], ~Op[4], ~Op[3], ~Op[2], Op[1], Op[0]);  // AND_Gate
  and and_41 (and_41_out, Op[5], ~Op[4], ~Op[3], Op[2], ~Op[1], ~Op[0]);  // AND_Gate
  and and_42 (and_42_out, Op[5], ~Op[4], ~Op[3], Op[2], ~Op[1], Op[0]);  // AND_Gate
  and and_43 (and_43_out, Op[5], ~Op[4], ~Op[3], Op[2], Op[1], ~Op[0]);  // AND_Gate
  and and_44 (and_44_out, Op[5], ~Op[4], ~Op[3], Op[2], Op[1], Op[0]);  // AND_Gate
  and and_45 (and_45_out, Op[5], ~Op[4], Op[3], ~Op[2], ~Op[1], ~Op[0]);  // AND_Gate
  and and_46 (and_46_out, Op[5], ~Op[4], Op[3], ~Op[2], ~Op[1], Op[0]);  // AND_Gate
  and and_47 (and_47_out, Op[5], ~Op[4], Op[3], ~Op[2], Op[1], ~Op[0]);  // AND_Gate
  and and_48 (and_48_out, Op[5], ~Op[4], Op[3], ~Op[2], Op[1], Op[0]);  // AND_Gate
  and and_49 (and_49_out, Op[5], ~Op[4], Op[3], Op[2], ~Op[1], ~Op[0]);  // AND_Gate
  and and_50 (and_50_out, Op[5], ~Op[4], Op[3], Op[2], ~Op[1], Op[0]);  // AND_Gate
  and and_51 (and_51_out, Op[5], ~Op[4], Op[3], Op[2], Op[1], ~Op[0]);  // AND_Gate
  and and_52 (and_52_out, Op[5], ~Op[4], Op[3], Op[2], Op[1], Op[0]);  // AND_Gate
  and and_53 (and_53_out, Op[5], Op[4], ~Op[3], ~Op[2], ~Op[1], ~Op[0]);  // AND_Gate
  and and_54 (and_54_out, Op[5], Op[4], ~Op[3], ~Op[2], ~Op[1], Op[0]);  // AND_Gate
  and and_55 (and_55_out, Op[5], Op[4], ~Op[3], ~Op[2], Op[1], ~Op[0]);  // AND_Gate
  and and_56 (and_56_out, Op[5], Op[4], ~Op[3], ~Op[2], Op[1], Op[0]);  // AND_Gate
  and and_57 (and_57_out, Op[5], Op[4], ~Op[3], Op[2], ~Op[1], ~Op[0]);  // AND_Gate
  and and_58 (and_58_out, Op[5], Op[4], ~Op[3], Op[2], ~Op[1], Op[0]);  // AND_Gate
  and and_59 (and_59_out, Op[5], Op[4], ~Op[3], Op[2], Op[1], ~Op[0]);  // AND_Gate
  and and_60 (and_60_out, Op[5], Op[4], ~Op[3], Op[2], Op[1], Op[0]);  // AND_Gate
  and and_61 (and_61_out, Op[5], Op[4], Op[3], ~Op[2], ~Op[1], ~Op[0]);  // AND_Gate
  and and_62 (and_62_out, Op[5], Op[4], Op[3], ~Op[2], ~Op[1], Op[0]);  // AND_Gate
  and and_63 (and_63_out, Op[5], Op[4], Op[3], ~Op[2], Op[1], ~Op[0]);  // AND_Gate
  and and_64 (and_64_out, Op[5], Op[4], Op[3], ~Op[2], Op[1], Op[0]);  // AND_Gate
  and and_65 (and_65_out, Op[5], Op[4], Op[3], Op[2], ~Op[1], ~Op[0]);  // AND_Gate
  and and_66 (and_66_out, Op[5], Op[4], Op[3], Op[2], ~Op[1], Op[0]);  // AND_Gate
  and and_67 (and_67_out, Op[5], Op[4], Op[3], Op[2], Op[1], ~Op[0]);  // AND_Gate
  and and_68 (and_68_out, Op[5], Op[4], Op[3], Op[2], Op[1], Op[0]);
  assign bit_extender_1_out = {{63{and_69_out}}, and_69_out};  // Bit_Extender bit_extender_1
  and and_69 (and_69_out, and_1_out, ~or_1_out);  // AND_Gate
  assign bit_extender_2_out = {{63{and_70_out}}, and_70_out};  // Bit_Extender bit_extender_2
  and and_70 (and_70_out, and_1_out, and_2_out);
  assign bit_extender_3_out = {{63{and_71_out}}, and_71_out};  // Bit_Extender bit_extender_3
  and and_71 (and_71_out, and_1_out, and_3_out);
  assign bit_extender_4_out = {{63{and_72_out}}, and_72_out};  // Bit_Extender bit_extender_4
  and and_72 (and_72_out, and_1_out, and_4_out);
  assign bit_extender_5_out = {{63{and_73_out}}, and_73_out};  // Bit_Extender bit_extender_5
  and and_73 (and_73_out, and_1_out, and_5_out);
  assign bit_extender_6_out = {{63{and_6_out}}, and_6_out};  // Bit_Extender bit_extender_6
  assign bit_extender_7_out = {{63{and_7_out}}, and_7_out};  // Bit_Extender bit_extender_7
  assign bit_extender_8_out = {{63{and_8_out}}, and_8_out};  // Bit_Extender bit_extender_8
  assign bit_extender_9_out = {{63{and_9_out}}, and_9_out};  // Bit_Extender bit_extender_9
  assign bit_extender_10_out = {{63{and_10_out}}, and_10_out};  // Bit_Extender bit_extender_10
  assign bit_extender_11_out = {{63{and_11_out}}, and_11_out};  // Bit_Extender bit_extender_11
  assign bit_extender_12_out = {{63{and_12_out}}, and_12_out};  // Bit_Extender bit_extender_12
  assign bit_extender_13_out = {{63{and_13_out}}, and_13_out};  // Bit_Extender bit_extender_13
  assign bit_extender_14_out = {{63{and_14_out}}, and_14_out};  // Bit_Extender bit_extender_14
  assign bit_extender_15_out = {{63{and_15_out}}, and_15_out};  // Bit_Extender bit_extender_15
  assign bit_extender_16_out = {{63{and_16_out}}, and_16_out};  // Bit_Extender bit_extender_16
  assign bit_extender_17_out = {{63{and_17_out}}, and_17_out};  // Bit_Extender bit_extender_17
  assign bit_extender_18_out = {{63{and_18_out}}, and_18_out};  // Bit_Extender bit_extender_18
  assign bit_extender_19_out = {{63{and_19_out}}, and_19_out};  // Bit_Extender bit_extender_19
  assign bit_extender_20_out = {{63{and_20_out}}, and_20_out};  // Bit_Extender bit_extender_20
  assign bit_extender_21_out = {{63{and_21_out}}, and_21_out};  // Bit_Extender bit_extender_21
  assign bit_extender_22_out = {{63{and_22_out}}, and_22_out};  // Bit_Extender bit_extender_22
  assign bit_extender_23_out = {{63{and_23_out}}, and_23_out};  // Bit_Extender bit_extender_23
  assign bit_extender_24_out = {{63{and_24_out}}, and_24_out};  // Bit_Extender bit_extender_24
  assign bit_extender_25_out = {{63{and_25_out}}, and_25_out};  // Bit_Extender bit_extender_25
  assign bit_extender_26_out = {{63{and_26_out}}, and_26_out};  // Bit_Extender bit_extender_26
  assign bit_extender_27_out = {{63{and_27_out}}, and_27_out};  // Bit_Extender bit_extender_27
  assign bit_extender_28_out = {{63{and_28_out}}, and_28_out};  // Bit_Extender bit_extender_28
  assign bit_extender_29_out = {{63{and_29_out}}, and_29_out};  // Bit_Extender bit_extender_29
  assign bit_extender_30_out = {{63{and_30_out}}, and_30_out};  // Bit_Extender bit_extender_30
  assign bit_extender_31_out = {{63{and_31_out}}, and_31_out};  // Bit_Extender bit_extender_31
  assign bit_extender_32_out = {{63{and_32_out}}, and_32_out};  // Bit_Extender bit_extender_32
  assign bit_extender_33_out = {{63{and_33_out}}, and_33_out};  // Bit_Extender bit_extender_33
  assign bit_extender_34_out = {{63{and_34_out}}, and_34_out};  // Bit_Extender bit_extender_34
  assign bit_extender_35_out = {{63{and_35_out}}, and_35_out};  // Bit_Extender bit_extender_35
  assign bit_extender_36_out = {{63{and_36_out}}, and_36_out};  // Bit_Extender bit_extender_36
  assign bit_extender_37_out = {{63{and_37_out}}, and_37_out};  // Bit_Extender bit_extender_37
  assign bit_extender_38_out = {{63{and_38_out}}, and_38_out};  // Bit_Extender bit_extender_38
  assign bit_extender_39_out = {{63{and_39_out}}, and_39_out};  // Bit_Extender bit_extender_39
  assign bit_extender_40_out = {{63{and_40_out}}, and_40_out};  // Bit_Extender bit_extender_40
  assign bit_extender_41_out = {{63{and_41_out}}, and_41_out};  // Bit_Extender bit_extender_41
  assign bit_extender_42_out = {{63{and_42_out}}, and_42_out};  // Bit_Extender bit_extender_42
  assign bit_extender_43_out = {{63{and_43_out}}, and_43_out};  // Bit_Extender bit_extender_43
  assign bit_extender_44_out = {{63{and_44_out}}, and_44_out};  // Bit_Extender bit_extender_44
  assign bit_extender_45_out = {{63{and_45_out}}, and_45_out};  // Bit_Extender bit_extender_45
  assign bit_extender_46_out = {{63{and_46_out}}, and_46_out};  // Bit_Extender bit_extender_46
  assign bit_extender_47_out = {{63{and_47_out}}, and_47_out};  // Bit_Extender bit_extender_47
  assign bit_extender_48_out = {{63{and_48_out}}, and_48_out};  // Bit_Extender bit_extender_48
  assign bit_extender_49_out = {{63{and_49_out}}, and_49_out};  // Bit_Extender bit_extender_49
  assign bit_extender_50_out = {{63{and_50_out}}, and_50_out};  // Bit_Extender bit_extender_50
  assign bit_extender_51_out = {{63{and_51_out}}, and_51_out};  // Bit_Extender bit_extender_51
  assign bit_extender_52_out = {{63{and_52_out}}, and_52_out};  // Bit_Extender bit_extender_52
  assign bit_extender_53_out = {{63{and_53_out}}, and_53_out};  // Bit_Extender bit_extender_53
  assign bit_extender_54_out = {{63{and_54_out}}, and_54_out};  // Bit_Extender bit_extender_54
  assign bit_extender_55_out = {{63{and_55_out}}, and_55_out};  // Bit_Extender bit_extender_55
  assign bit_extender_56_out = {{63{and_56_out}}, and_56_out};  // Bit_Extender bit_extender_56
  assign bit_extender_57_out = {{63{and_57_out}}, and_57_out};  // Bit_Extender bit_extender_57
  assign bit_extender_58_out = {{63{and_58_out}}, and_58_out};  // Bit_Extender bit_extender_58
  assign bit_extender_59_out = {{63{and_59_out}}, and_59_out};  // Bit_Extender bit_extender_59
  assign bit_extender_60_out = {{63{and_60_out}}, and_60_out};  // Bit_Extender bit_extender_60
  assign bit_extender_61_out = {{63{and_61_out}}, and_61_out};  // Bit_Extender bit_extender_61
  assign bit_extender_62_out = {{63{and_62_out}}, and_62_out};  // Bit_Extender bit_extender_62
  assign bit_extender_63_out = {{63{and_63_out}}, and_63_out};  // Bit_Extender bit_extender_63
  assign bit_extender_64_out = {{63{and_64_out}}, and_64_out};  // Bit_Extender bit_extender_64
  assign bit_extender_65_out = {{63{and_65_out}}, and_65_out};  // Bit_Extender bit_extender_65
  assign bit_extender_66_out = {{63{and_66_out}}, and_66_out};  // Bit_Extender bit_extender_66
  assign bit_extender_67_out = {{63{and_67_out}}, and_67_out};  // Bit_Extender bit_extender_67
  assign bit_extender_68_out = {{63{and_68_out}}, and_68_out};  // Bit_Extender bit_extender_68
  assign and_74_out = 64'h10081 & bit_extender_1_out;  // AND_Gate and_74, 64 bits wide
  assign and_75_out = 64'h200 & bit_extender_2_out;  // AND_Gate and_75, 64 bits wide
  assign and_76_out = 64'h1c200 & bit_extender_3_out;  // AND_Gate and_76, 64 bits wide
  assign and_77_out = 64'h1c000 & bit_extender_4_out;  // AND_Gate and_77, 64 bits wide
  assign and_78_out = 64'h10089 & bit_extender_5_out;  // AND_Gate and_78, 64 bits wide
  assign and_79_out = {64{1'b0}} & bit_extender_6_out;  // AND_Gate and_79, 64 bits wide
  assign and_80_out = 64'h200 & bit_extender_7_out;  // AND_Gate and_80, 64 bits wide
  assign and_81_out = 64'h1c200 & bit_extender_8_out;  // AND_Gate and_81, 64 bits wide
  assign and_82_out = 64'h100 & bit_extender_9_out;  // AND_Gate and_82, 64 bits wide
  assign and_83_out = 64'h100 & bit_extender_10_out;  // AND_Gate and_83, 64 bits wide
  assign and_84_out = 64'h300 & bit_extender_11_out;  // AND_Gate and_84, 64 bits wide
  assign and_85_out = 64'h300 & bit_extender_12_out;  // AND_Gate and_85, 64 bits wide
  assign and_86_out = 64'h10002 & bit_extender_13_out;  // AND_Gate and_86, 64 bits wide
  assign and_87_out = 64'h10012 & bit_extender_14_out;  // AND_Gate and_87, 64 bits wide
  assign and_88_out = 64'h10032 & bit_extender_15_out;  // AND_Gate and_88, 64 bits wide
  assign and_89_out = 64'h10042 & bit_extender_16_out;  // AND_Gate and_89, 64 bits wide
  assign and_90_out = 64'h10054 & bit_extender_17_out;  // AND_Gate and_90, 64 bits wide
  assign and_91_out = 64'h10064 & bit_extender_18_out;  // AND_Gate and_91, 64 bits wide
  assign and_92_out = 64'h10074 & bit_extender_19_out;  // AND_Gate and_92, 64 bits wide
  assign and_93_out = 64'h18000 & bit_extender_20_out;  // AND_Gate and_93, 64 bits wide
  assign and_94_out = {64{1'b0}} & bit_extender_21_out;  // AND_Gate and_94, 64 bits wide
  assign and_95_out = {64{1'b0}} & bit_extender_22_out;  // AND_Gate and_95, 64 bits wide
  assign and_96_out = {64{1'b0}} & bit_extender_23_out;  // AND_Gate and_96, 64 bits wide
  assign and_97_out = {64{1'b0}} & bit_extender_24_out;  // AND_Gate and_97, 64 bits wide
  assign and_98_out = {64{1'b0}} & bit_extender_25_out;  // AND_Gate and_98, 64 bits wide
  assign and_99_out = {64{1'b0}} & bit_extender_26_out;  // AND_Gate and_99, 64 bits wide
  assign and_100_out = {64{1'b0}} & bit_extender_27_out;  // AND_Gate and_100, 64 bits wide
  assign and_101_out = {64{1'b0}} & bit_extender_28_out;  // AND_Gate and_101, 64 bits wide
  assign and_102_out = {64{1'b0}} & bit_extender_29_out;  // AND_Gate and_102, 64 bits wide
  assign and_103_out = {64{1'b0}} & bit_extender_30_out;  // AND_Gate and_103, 64 bits wide
  assign and_104_out = {64{1'b0}} & bit_extender_31_out;  // AND_Gate and_104, 64 bits wide
  assign and_105_out = {64{1'b0}} & bit_extender_32_out;  // AND_Gate and_105, 64 bits wide
  assign and_106_out = {64{1'b0}} & bit_extender_33_out;  // AND_Gate and_106, 64 bits wide
  assign and_107_out = {64{1'b0}} & bit_extender_34_out;  // AND_Gate and_107, 64 bits wide
  assign and_108_out = {64{1'b0}} & bit_extender_35_out;  // AND_Gate and_108, 64 bits wide
  assign and_109_out = {64{1'b0}} & bit_extender_36_out;  // AND_Gate and_109, 64 bits wide
  assign and_110_out = 64'h14002 & bit_extender_37_out;  // AND_Gate and_110, 64 bits wide
  assign and_111_out = 64'h14402 & bit_extender_38_out;  // AND_Gate and_111, 64 bits wide
  assign and_112_out = 64'h15802 & bit_extender_39_out;  // AND_Gate and_112, 64 bits wide
  assign and_113_out = 64'h14802 & bit_extender_40_out;  // AND_Gate and_113, 64 bits wide
  assign and_114_out = 64'h15002 & bit_extender_41_out;  // AND_Gate and_114, 64 bits wide
  assign and_115_out = 64'h15402 & bit_extender_42_out;  // AND_Gate and_115, 64 bits wide
  assign and_116_out = 64'h15c02 & bit_extender_43_out;  // AND_Gate and_116, 64 bits wide
  assign and_117_out = {64{1'b0}} & bit_extender_44_out;  // AND_Gate and_117, 64 bits wide
  assign and_118_out = 64'h2002 & bit_extender_45_out;  // AND_Gate and_118, 64 bits wide
  assign and_119_out = 64'h2402 & bit_extender_46_out;  // AND_Gate and_119, 64 bits wide
  assign and_120_out = 64'h3802 & bit_extender_47_out;  // AND_Gate and_120, 64 bits wide
  assign and_121_out = 64'h2802 & bit_extender_48_out;  // AND_Gate and_121, 64 bits wide
  assign and_122_out = {64{1'b0}} & bit_extender_49_out;  // AND_Gate and_122, 64 bits wide
  assign and_123_out = {64{1'b0}} & bit_extender_50_out;  // AND_Gate and_123, 64 bits wide
  assign and_124_out = 64'h3c02 & bit_extender_51_out;  // AND_Gate and_124, 64 bits wide
  assign and_125_out = {64{1'b0}} & bit_extender_52_out;  // AND_Gate and_125, 64 bits wide
  assign and_126_out = {64{1'b0}} & bit_extender_53_out;  // AND_Gate and_126, 64 bits wide
  assign and_127_out = {64{1'b0}} & bit_extender_54_out;  // AND_Gate and_127, 64 bits wide
  assign and_128_out = {64{1'b0}} & bit_extender_55_out;  // AND_Gate and_128, 64 bits wide
  assign and_129_out = {64{1'b0}} & bit_extender_56_out;  // AND_Gate and_129, 64 bits wide
  assign and_130_out = {64{1'b0}} & bit_extender_57_out;  // AND_Gate and_130, 64 bits wide
  assign and_131_out = {64{1'b0}} & bit_extender_58_out;  // AND_Gate and_131, 64 bits wide
  assign and_132_out = {64{1'b0}} & bit_extender_59_out;  // AND_Gate and_132, 64 bits wide
  assign and_133_out = {64{1'b0}} & bit_extender_60_out;  // AND_Gate and_133, 64 bits wide
  assign and_134_out = {64{1'b0}} & bit_extender_61_out;  // AND_Gate and_134, 64 bits wide
  assign and_135_out = {64{1'b0}} & bit_extender_62_out;  // AND_Gate and_135, 64 bits wide
  assign and_136_out = {64{1'b0}} & bit_extender_63_out;  // AND_Gate and_136, 64 bits wide
  assign and_137_out = {64{1'b0}} & bit_extender_64_out;  // AND_Gate and_137, 64 bits wide
  assign and_138_out = {64{1'b0}} & bit_extender_65_out;  // AND_Gate and_138, 64 bits wide
  assign and_139_out = {64{1'b0}} & bit_extender_66_out;  // AND_Gate and_139, 64 bits wide
  assign and_140_out = {64{1'b0}} & bit_extender_67_out;  // AND_Gate and_140, 64 bits wide
  assign and_141_out = {64{1'b0}} & bit_extender_68_out;  // AND_Gate and_141, 64 bits wide
  assign {or_5_out, RegWrite, RegWriteDataSrc, MemOp, BranchOp, ALUOp, ALUSrcA, ALUSrcB, WriteRegSrc} = and_74_out | or_6_out;  // OR_Gate or_5, 64 bits wide
  assign or_6_out = and_75_out | or_7_out;  // OR_Gate or_6, 64 bits wide
  assign or_7_out = and_76_out | or_8_out;  // OR_Gate or_7, 64 bits wide
  assign or_8_out = and_77_out | or_9_out;  // OR_Gate or_8, 64 bits wide
  assign or_9_out = and_78_out | or_10_out;  // OR_Gate or_9, 64 bits wide
  assign or_10_out = and_79_out | or_11_out;  // OR_Gate or_10, 64 bits wide
  assign or_11_out = and_80_out | or_12_out;  // OR_Gate or_11, 64 bits wide
  assign or_12_out = and_81_out | or_13_out;  // OR_Gate or_12, 64 bits wide
  assign or_13_out = and_82_out | or_14_out;  // OR_Gate or_13, 64 bits wide
  assign or_14_out = and_83_out | or_15_out;  // OR_Gate or_14, 64 bits wide
  assign or_15_out = and_84_out | or_16_out;  // OR_Gate or_15, 64 bits wide
  assign or_16_out = and_85_out | or_17_out;  // OR_Gate or_16, 64 bits wide
  assign or_17_out = and_86_out | or_18_out;  // OR_Gate or_17, 64 bits wide
  assign or_18_out = and_87_out | or_19_out;  // OR_Gate or_18, 64 bits wide
  assign or_19_out = and_88_out | or_20_out;  // OR_Gate or_19, 64 bits wide
  assign or_20_out = and_89_out | or_21_out;  // OR_Gate or_20, 64 bits wide
  assign or_21_out = and_90_out | or_22_out;  // OR_Gate or_21, 64 bits wide
  assign or_22_out = and_91_out | or_23_out;  // OR_Gate or_22, 64 bits wide
  assign or_23_out = and_92_out | or_24_out;  // OR_Gate or_23, 64 bits wide
  assign or_24_out = and_93_out | or_25_out;  // OR_Gate or_24, 64 bits wide
  assign or_25_out = and_94_out | or_26_out;  // OR_Gate or_25, 64 bits wide
  assign or_26_out = and_95_out | or_27_out;  // OR_Gate or_26, 64 bits wide
  assign or_27_out = and_96_out | or_28_out;  // OR_Gate or_27, 64 bits wide
  assign or_28_out = and_97_out | or_29_out;  // OR_Gate or_28, 64 bits wide
  assign or_29_out = and_98_out | or_30_out;  // OR_Gate or_29, 64 bits wide
  assign or_30_out = and_99_out | or_31_out;  // OR_Gate or_30, 64 bits wide
  assign or_31_out = and_100_out | or_32_out;  // OR_Gate or_31, 64 bits wide
  assign or_32_out = and_101_out | or_33_out;  // OR_Gate or_32, 64 bits wide
  assign or_33_out = and_102_out | or_34_out;  // OR_Gate or_33, 64 bits wide
  assign or_34_out = and_103_out | or_35_out;  // OR_Gate or_34, 64 bits wide
  assign or_35_out = and_104_out | or_36_out;  // OR_Gate or_35, 64 bits wide
  assign or_36_out = and_105_out | or_37_out;  // OR_Gate or_36, 64 bits wide
  assign or_37_out = and_106_out | or_38_out;  // OR_Gate or_37, 64 bits wide
  assign or_38_out = and_107_out | or_39_out;  // OR_Gate or_38, 64 bits wide
  assign or_39_out = and_108_out | or_40_out;  // OR_Gate or_39, 64 bits wide
  assign or_40_out = and_109_out | or_41_out;  // OR_Gate or_40, 64 bits wide
  assign or_41_out = and_110_out | or_42_out;  // OR_Gate or_41, 64 bits wide
  assign or_42_out = and_111_out | or_43_out;  // OR_Gate or_42, 64 bits wide
  assign or_43_out = and_112_out | or_44_out;  // OR_Gate or_43, 64 bits wide
  assign or_44_out = and_113_out | or_45_out;  // OR_Gate or_44, 64 bits wide
  assign or_45_out = and_114_out | or_46_out;  // OR_Gate or_45, 64 bits wide
  assign or_46_out = and_115_out | or_47_out;  // OR_Gate or_46, 64 bits wide
  assign or_47_out = and_116_out | or_48_out;  // OR_Gate or_47, 64 bits wide
  assign or_48_out = and_117_out | or_49_out;  // OR_Gate or_48, 64 bits wide
  assign or_49_out = and_118_out | or_50_out;  // OR_Gate or_49, 64 bits wide
  assign or_50_out = and_119_out | or_51_out;  // OR_Gate or_50, 64 bits wide
  assign or_51_out = and_120_out | or_52_out;  // OR_Gate or_51, 64 bits wide
  assign or_52_out = and_121_out | or_53_out;  // OR_Gate or_52, 64 bits wide
  assign or_53_out = and_122_out | or_54_out;  // OR_Gate or_53, 64 bits wide
  assign or_54_out = and_123_out | or_55_out;  // OR_Gate or_54, 64 bits wide
  assign or_55_out = and_124_out | or_56_out;  // OR_Gate or_55, 64 bits wide
  assign or_56_out = and_125_out | or_57_out;  // OR_Gate or_56, 64 bits wide
  assign or_57_out = and_126_out | or_58_out;  // OR_Gate or_57, 64 bits wide
  assign or_58_out = and_127_out | or_59_out;  // OR_Gate or_58, 64 bits wide
  assign or_59_out = and_128_out | or_60_out;  // OR_Gate or_59, 64 bits wide
  assign or_60_out = and_129_out | or_61_out;  // OR_Gate or_60, 64 bits wide
  assign or_61_out = and_130_out | or_62_out;  // OR_Gate or_61, 64 bits wide
  assign or_62_out = and_131_out | or_63_out;  // OR_Gate or_62, 64 bits wide
  assign or_63_out = and_132_out | or_64_out;  // OR_Gate or_63, 64 bits wide
  assign or_64_out = and_133_out | or_65_out;  // OR_Gate or_64, 64 bits wide
  assign or_65_out = and_134_out | or_66_out;  // OR_Gate or_65, 64 bits wide
  assign or_66_out = and_135_out | or_67_out;  // OR_Gate or_66, 64 bits wide
  assign or_67_out = and_136_out | or_68_out;  // OR_Gate or_67, 64 bits wide
  assign or_68_out = and_137_out | or_69_out;  // OR_Gate or_68, 64 bits wide
  assign or_69_out = and_138_out | or_70_out;  // OR_Gate or_69, 64 bits wide
  assign or_70_out = and_139_out | or_71_out;  // OR_Gate or_70, 64 bits wide
  assign or_71_out = and_140_out | or_72_out;  // OR_Gate or_71, 64 bits wide
  assign or_72_out = and_141_out | {64{1'b0}};  // OR_Gate or_72, 64 bits wide
  // NoConnect on undriven

  // Notes on the sheet:
  //   This circuit performs the primary decoding of instructions into control
  //   path values. Existing within the Control Unit, this circuit maps instructions
  //   (primarily by OP code) to values which control operations on the data path.
  //   Note that some outputs of the Main Decoder (namely ALUOp and BranchOp)
  //   are processed further by the Control Unit before being passed to the control
  //   path.
  //   Existing in the Decode (D) stage within the Control Unit, the Main Decoder
  //   takes the current instruction in the Decode (D) stage's Op and Funct codes
  //   and maps them to an assortment of control path values and intermediary
  //   values--which are turned into control path values by the rest of the Control Unit.
  //   Note that the Main Decoder only uses Funct values to override certain outputs
  //   for select R-Type (Op == 0) instructions.  The primary decoding of an instruction's
  //   Funct value occurs inside the ALU Decoder when an ALUOp code of 1xxx is output
  //   by the Main Decoder.
  //   OP: 0
  //   Overrides:
  //   Funct: 0b001000
  //   Funct: 0b001001
  //   Funct: 0b001100
  //   Funct: 0b0000xx
  //   OP: 1
  //   OP: 2
  //   OP: 3
  //   OP: 4
  //   OP: 5
  //   OP: 6
  //   OP: 7
  //   OP: 8
  //   OP: 9
  //   OP: 10
  //   OP: 11
  //   OP: 12
  //   OP: 13
  //   OP: 14
  //   OP: 15
  //   OP: 16
  //   OP: 17
  //   OP: 18
  //   OP: 19
  //   OP: 20
  //   OP: 21
  //   OP: 22
  //   OP: 23
  //   OP: 24
  //   OP: 25
  //   OP: 26
  //   OP: 27
  //   OP: 28
  //   OP: 29
  //   OP: 30
  //   OP: 31
  //   OP: 32
  //   OP: 33
  //   OP: 34
  //   OP: 35
  //   OP: 36
  //   OP: 37
  //   OP: 38
  //   OP: 39
  //   OP: 40
  //   OP: 41
  //   OP: 42
  //   OP: 43
  //   OP: 44
  //   OP: 45
  //   OP: 46
  //   OP: 47
  //   OP: 48
  //   OP: 49
  //   OP: 50
  //   OP: 51
  //   OP: 52
  //   OP: 53
  //   OP: 54
  //   OP: 55
  //   OP: 56
  //   OP: 57
  //   OP: 58
  //   OP: 59
  //   OP: 60
  //   OP: 61
  //   OP: 62
  //   OP: 63
  //   Main Decoder
  //   R-Type Overrides
  //   0 - No write to register
  //   1 - Write to register in Writeback (W) stage
  //   00 - WriteData == ALUOut
  //   01 - WriteData == ReadData (memory)
  //   10 - WriteData == UpperImm
  //   11 - WriteData == PCPlus4 and WriteReg == $ra
  //   MemOp Codes:
  //   0000 - lb
  //   0001 - lh
  //   0010 - lw
  //   0011 - N/A
  //   0100 - lbu
  //   0101 - lhu
  //   0110 - lwl
  //   0111 - lwr
  //   00 - No Branch/Jump
  //   01 - beq/bne conditional branch to BTA
  //   10 - jump to JTA (Jump Target Address)
  //   11 - blez/bgtz conditional branch to BTA
  //   1-00-0000-00-1000-0-00-1
  //   0-00-0000-10-0000-0-00-0
  //   1-11-0000-10-0000-0-00-0
  //   1-11-0000-00-0000-0-00-0
  //   1-00-0000-00-1000-1-00-1
  //   0-00-0000-10-0000-0-00-0
  //   1-11-0000-10-0000-0-00-0
  //   0-00-0000-01-0000-0-00-0
  //   0-00-0000-01-0000-0-00-0
  //   0-00-0000-11-0000-0-00-0
  //   0-00-0000-11-0000-0-00-0
  //   1-00-0000-00-0000-0-01-0
  //   1-00-0000-00-0001-0-01-0
  //   1-00-0000-00-0011-0-01-0
  //   1-00-0000-00-0100-0-01-0
  //   1-00-0000-00-0101-0-10-0
  //   1-00-0000-00-0110-0-10-0
  //   1-00-0000-00-0111-0-10-0
  //   1-10-0000-00-0000-0-00-0
  //   not yet implemented
  //   1-01-0000-00-0000-0-01-0
  //   1-01-0001-00-0000-0-01-0
  //   1-01-0110-00-0000-0-01-0
  //   1-01-0010-00-0000-0-01-0
  //   1-01-0100-00-0000-0-01-0
  //   1-01-0101-00-0000-0-01-0
  //   1-01-0111-00-0000-0-01-0
  //   0-00-1000-00-0000-0-01-0
  //   0-00-1001-00-0000-0-01-0
  //   0-00-1110-00-0000-0-01-0
  //   0-00-1010-00-0000-0-01-0
  //   0-00-1111-00-0000-0-01-0
  //   not yet implemented
  //   not yet implemented
  //   not yet implemented
  //   not yet implemented
  //   not yet implemented
  //   not yet implemented
  //   not yet implemented
  //   not yet implemented
  //   not yet implemented
  //   not yet implemented
  //   not yet implemented
  //   not yet implemented
  //   RegWrite Codes:
  //   RegWriteDataSrc Codes:
  //   BranchOp Codes:
  //   R-Type
  //   jr
  //   jral
  //   syscall
  //   sll/srl/sra
  //   j
  //   jal
  //   beq
  //   bne
  //   blez
  //   bgtz
  //   addi
  //   addiu
  //   slti
  //   sltiu
  //   andi
  //   ori
  //   xori
  //   lui
  //   F-Type
  //   RESERVED FOR KERNEL
  //   SUSPENDS PROCESSOR
  //   RESERVED FOR KERNEL
  //   PRINT CHAR ($a0)
  //   lb
  //   lh
  //   lwl
  //   lw
  //   lbu
  //   lhu
  //   lwr
  //   sb
  //   sh
  //   swl
  //   sw
  //   swr
  //   cache
  //   ll
  //   lwc1
  //   lwc2
  //   pref
  //   ldc1
  //   ldc2
  //   sc
  //   swc1
  //   swc2
  //   sdc1
  //   sdc2
  //   1000 - sb
  //   1001 - sh
  //   1010 - sw
  //   1011 - N/A
  //   1100 - N/A
  //   1101 - N/A
  //   1110 - swl
  //   1111 - swr
  //   The following reserved OP codes are not
  //   to be directly used within user programs...
  //   Lower output values are used by the main circuit's data path before higher output
  //   values. Bottom values are used in the Execute (E) stage while the top values are
  //   used in the Writeback (W) stage.
  //   An output value may be used in an earlier stage, but its placement here depends on the
  //   furthest point along the pipeline where the value is used.
  //   The constant passed into the AND gate associated with any of these binary
  //   strings is the zero-extended numerical representation of the string's binary value
  //   (excluding any '-' characters) with the first bit being the most significant bit.
  //   Updating the constant is done by typing "0bxxxx..." into its value field, where
  //   "xxx..." is the binary string without any '-' characters.
  //   ALUOp Codes:
  //   0000 - add
  //   0001 - addu
  //   0010 - subu
  //   0011 - slt
  //   0100 - sltu
  //   0101 - and
  //   0110 - or
  //   0111 - xor
  //   1xxx - Look at Funct
  //   ALUSrcA Codes:
  //   0 - ALUInputA = RegData1
  //   1 - ALUInputA = shamt (Zero-Extended)
  //   ALUSrcB Codes:
  //   00 - ALUInputB = RegData2
  //   x1 - ALUInputB = SignImm
  //   10 - ALUInputB = ZeroImm
  //   0 - WriteReg = rt
  //   1 - WriteReg = rd
  //   (RegWrite-RegWriteDataSrc-. . .-ALUSrcB-WriteRegSrc)
  //   Main Decoder output for its associated instruction.
  //   WriteRegSrc Codes:
  //   Outputs
  //   <- Output values are sorted (bottom-up) in the order used by the main circuit (left-to-right).
  //   Binary String Labels
  //   <--  Each '-' separated binary value is an output value (in order of circuit outputs).
  //   The entire binary string with '-' separators describes the intended
endmodule

module ALUDecoder (
  input  [3:0] ALUOp,
  input  [5:0] Funct,
  output NOT_ALUOut,
  output [4:0] ALUControl
);

  wire and_1_out, and_2_out, and_3_out, and_4_out, and_6_out, and_7_out, and_8_out, and_9_out, and_10_out,
       and_11_out, and_12_out, and_13_out, and_14_out, and_15_out, and_16_out, and_17_out, and_18_out,
       and_19_out, and_20_out, and_21_out, and_22_out, and_23_out, and_24_out, and_25_out, and_26_out,
       and_27_out, and_28_out, and_29_out, or_1_out, or_2_out, or_3_out, or_4_out, or_5_out, or_6_out,
       or_7_out, or_8_out, or_9_out, or_10_out, or_11_out, or_12_out, or_13_out;
  wire [4:0] and_30_out, and_31_out, and_32_out, and_33_out, and_34_out, and_35_out, and_36_out, and_37_out,
       and_38_out, and_39_out, and_40_out, and_41_out, and_42_out, and_43_out, and_44_out, and_45_out,
       and_46_out, and_47_out, and_48_out, and_49_out, bit_extender_1_out, bit_extender_2_out,
       bit_extender_3_out, bit_extender_4_out, bit_extender_5_out, bit_extender_6_out, bit_extender_7_out,
       bit_extender_8_out, bit_extender_9_out, bit_extender_10_out, bit_extender_11_out, bit_extender_12_out,
       bit_extender_13_out, bit_extender_14_out, bit_extender_15_out, bit_extender_16_out,
       bit_extender_17_out, bit_extender_18_out, bit_extender_19_out, bit_extender_20_out, or_15_out,
       or_16_out, or_17_out, or_18_out, or_19_out, or_20_out, or_21_out, or_22_out, or_23_out, or_24_out,
       or_25_out, or_26_out, or_27_out, or_28_out, or_29_out, or_30_out, or_31_out, or_32_out, or_33_out;

  and and_1 (and_1_out, ~ALUOp[3], ALUOp[2], ~ALUOp[1], ALUOp[0]);  // AND_Gate
  and and_2 (and_2_out, Funct[5], ~Funct[4], ~Funct[3], Funct[2], ~Funct[1], ~Funct[0], ALUOp[3]);  // AND_Gate
  and and_3 (and_3_out, ~ALUOp[3], ALUOp[2], ALUOp[1], ~ALUOp[0]);  // AND_Gate
  and and_4 (and_4_out, Funct[5], ~Funct[4], ~Funct[3], Funct[2], ~Funct[1], Funct[0], ALUOp[3]);  // AND_Gate
  and and_5 (NOT_ALUOut, Funct[5], ~Funct[4], ~Funct[3], Funct[2], Funct[1], Funct[0], ALUOp[3]);  // AND_Gate
  and and_6 (and_6_out, ~ALUOp[3], ALUOp[2], ALUOp[1], ALUOp[0]);  // AND_Gate
  and and_7 (and_7_out, Funct[5], ~Funct[4], ~Funct[3], ~Funct[2], ~Funct[1], ~Funct[0], ALUOp[3]);  // AND_Gate
  and and_8 (and_8_out, ~Funct[5], ~Funct[4], ~Funct[3], ~Funct[1], ~Funct[0], ALUOp[3]);  // AND_Gate
  and and_9 (and_9_out, ~Funct[5], ~Funct[4], ~Funct[3], Funct[1], ~Funct[0], ALUOp[3]);  // AND_Gate
  and and_10 (and_10_out, ~Funct[5], ~Funct[4], ~Funct[3], Funct[1], Funct[0], ALUOp[3]);  // AND_Gate
  and and_11 (and_11_out, ~ALUOp[3], ~ALUOp[2], ~ALUOp[1], ~ALUOp[0]);  // AND_Gate
  and and_12 (and_12_out, Funct[5], ~Funct[4], ~Funct[3], ~Funct[2], ~Funct[1], ~Funct[0], ALUOp[3]);  // AND_Gate
  and and_13 (and_13_out, ~ALUOp[3], ~ALUOp[2], ~ALUOp[1], ALUOp[0]);  // AND_Gate
  and and_14 (and_14_out, Funct[5], ~Funct[4], ~Funct[3], ~Funct[2], ~Funct[1], Funct[0], ALUOp[3]);  // AND_Gate
  and and_15 (and_15_out, Funct[5], ~Funct[4], ~Funct[3], ~Funct[2], Funct[1], ~Funct[0], ALUOp[3]);  // AND_Gate
  and and_16 (and_16_out, ~ALUOp[3], ~ALUOp[2], ALUOp[1], ~ALUOp[0]);  // AND_Gate
  and and_17 (and_17_out, Funct[5], ~Funct[4], ~Funct[3], ~Funct[2], Funct[1], Funct[0], ALUOp[3]);  // AND_Gate
  and and_18 (and_18_out, ~Funct[5], Funct[4], Funct[3], ~Funct[2], ~Funct[1], ~Funct[0], ALUOp[3]);  // AND_Gate
  and and_19 (and_19_out, ~Funct[5], Funct[4], Funct[3], ~Funct[2], ~Funct[1], Funct[0], ALUOp[3]);  // AND_Gate
  and and_20 (and_20_out, ~Funct[5], Funct[4], Funct[3], ~Funct[2], Funct[1], ~Funct[0], ALUOp[3]);  // AND_Gate
  and and_21 (and_21_out, ~Funct[5], Funct[4], Funct[3], ~Funct[2], Funct[1], Funct[0], ALUOp[3]);  // AND_Gate
  and and_22 (and_22_out, ~ALUOp[3], ~ALUOp[2], ALUOp[1], ALUOp[0]);  // AND_Gate
  and and_23 (and_23_out, Funct[5], ~Funct[4], Funct[3], ~Funct[2], Funct[1], ~Funct[0], ALUOp[3]);  // AND_Gate
  and and_24 (and_24_out, ~ALUOp[3], ALUOp[2], ~ALUOp[1], ~ALUOp[0]);  // AND_Gate
  and and_25 (and_25_out, Funct[5], ~Funct[4], Funct[3], ~Funct[2], Funct[1], Funct[0], ALUOp[3]);  // AND_Gate
  and and_26 (and_26_out, ~Funct[5], Funct[4], ~Funct[3], ~Funct[2], ~Funct[1], ~Funct[0], ALUOp[3]);  // AND_Gate
  and and_27 (and_27_out, ~Funct[5], Funct[4], ~Funct[3], ~Funct[2], ~Funct[1], Funct[0], ALUOp[3]);  // AND_Gate
  and and_28 (and_28_out, ~Funct[5], Funct[4], ~Funct[3], ~Funct[2], Funct[1], ~Funct[0], ALUOp[3]);  // AND_Gate
  and and_29 (and_29_out, ~Funct[5], Funct[4], ~Funct[3], ~Funct[2], Funct[1], Funct[0], ALUOp[3]);  // AND_Gate
  or or_1 (or_1_out, and_1_out, and_2_out);
  or or_2 (or_2_out, and_3_out, and_4_out, NOT_ALUOut);
  or or_3 (or_3_out, and_6_out, and_7_out);
  or or_4 (or_4_out, and_11_out, and_12_out);
  or or_5 (or_5_out, and_13_out, and_14_out);
  buf or_6 (or_6_out, and_15_out);  // OR_Gate
  or or_7 (or_7_out, and_16_out, and_17_out);
  buf or_8 (or_8_out, and_18_out);  // OR_Gate
  buf or_9 (or_9_out, and_19_out);  // OR_Gate
  buf or_10 (or_10_out, and_20_out);  // OR_Gate
  buf or_11 (or_11_out, and_21_out);  // OR_Gate
  or or_12 (or_12_out, and_22_out, and_23_out);
  or or_13 (or_13_out, and_24_out, and_25_out);
  assign bit_extender_1_out = {{4{or_1_out}}, or_1_out};  // Bit_Extender bit_extender_1
  assign bit_extender_2_out = {{4{or_2_out}}, or_2_out};  // Bit_Extender bit_extender_2
  assign bit_extender_3_out = {{4{or_3_out}}, or_3_out};  // Bit_Extender bit_extender_3
  assign bit_extender_4_out = {{4{and_8_out}}, and_8_out};  // Bit_Extender bit_extender_4
  assign bit_extender_5_out = {{4{and_9_out}}, and_9_out};  // Bit_Extender bit_extender_5
  assign bit_extender_6_out = {{4{and_10_out}}, and_10_out};  // Bit_Extender bit_extender_6
  assign bit_extender_7_out = {{4{or_4_out}}, or_4_out};  // Bit_Extender bit_extender_7
  assign bit_extender_8_out = {{4{or_5_out}}, or_5_out};  // Bit_Extender bit_extender_8
  assign bit_extender_9_out = {{4{or_6_out}}, or_6_out};  // Bit_Extender bit_extender_9
  assign bit_extender_10_out = {{4{or_7_out}}, or_7_out};  // Bit_Extender bit_extender_10
  assign bit_extender_11_out = {{4{or_8_out}}, or_8_out};  // Bit_Extender bit_extender_11
  assign bit_extender_12_out = {{4{or_9_out}}, or_9_out};  // Bit_Extender bit_extender_12
  assign bit_extender_13_out = {{4{or_10_out}}, or_10_out};  // Bit_Extender bit_extender_13
  assign bit_extender_14_out = {{4{or_11_out}}, or_11_out};  // Bit_Extender bit_extender_14
  assign bit_extender_15_out = {{4{or_12_out}}, or_12_out};  // Bit_Extender bit_extender_15
  assign bit_extender_16_out = {{4{or_13_out}}, or_13_out};  // Bit_Extender bit_extender_16
  assign bit_extender_17_out = {{4{and_26_out}}, and_26_out};  // Bit_Extender bit_extender_17
  assign bit_extender_18_out = {{4{and_27_out}}, and_27_out};  // Bit_Extender bit_extender_18
  assign bit_extender_19_out = {{4{and_28_out}}, and_28_out};  // Bit_Extender bit_extender_19
  assign bit_extender_20_out = {{4{and_29_out}}, and_29_out};  // Bit_Extender bit_extender_20
  assign and_30_out = {5{1'b0}} & bit_extender_1_out;  // AND_Gate and_30, 5 bits wide
  assign and_31_out = 5'b00001 & bit_extender_2_out;  // AND_Gate and_31, 5 bits wide
  assign and_32_out = 5'b00010 & bit_extender_3_out;  // AND_Gate and_32, 5 bits wide
  assign and_33_out = 5'b00011 & bit_extender_4_out;  // AND_Gate and_33, 5 bits wide
  assign and_34_out = 5'b00100 & bit_extender_5_out;  // AND_Gate and_34, 5 bits wide
  assign and_35_out = 5'b00101 & bit_extender_6_out;  // AND_Gate and_35, 5 bits wide
  assign and_36_out = 5'b00110 & bit_extender_7_out;  // AND_Gate and_36, 5 bits wide
  assign and_37_out = 5'b00111 & bit_extender_8_out;  // AND_Gate and_37, 5 bits wide
  assign and_38_out = 5'b01000 & bit_extender_9_out;  // AND_Gate and_38, 5 bits wide
  assign and_39_out = 5'b01001 & bit_extender_10_out;  // AND_Gate and_39, 5 bits wide
  assign and_40_out = 5'b01010 & bit_extender_11_out;  // AND_Gate and_40, 5 bits wide
  assign and_41_out = 5'b01011 & bit_extender_12_out;  // AND_Gate and_41, 5 bits wide
  assign and_42_out = 5'b01100 & bit_extender_13_out;  // AND_Gate and_42, 5 bits wide
  assign and_43_out = 5'b01101 & bit_extender_14_out;  // AND_Gate and_43, 5 bits wide
  assign and_44_out = 5'b01110 & bit_extender_15_out;  // AND_Gate and_44, 5 bits wide
  assign and_45_out = 5'b01111 & bit_extender_16_out;  // AND_Gate and_45, 5 bits wide
  assign and_46_out = 5'b10000 & bit_extender_17_out;  // AND_Gate and_46, 5 bits wide
  assign and_47_out = 5'b10001 & bit_extender_18_out;  // AND_Gate and_47, 5 bits wide
  assign and_48_out = 5'b10010 & bit_extender_19_out;  // AND_Gate and_48, 5 bits wide
  assign and_49_out = 5'b10011 & bit_extender_20_out;  // AND_Gate and_49, 5 bits wide
  assign ALUControl = and_30_out | or_15_out;  // OR_Gate or_14, 5 bits wide
  assign or_15_out = and_31_out | or_16_out;  // OR_Gate or_15, 5 bits wide
  assign or_16_out = and_32_out | or_17_out;  // OR_Gate or_16, 5 bits wide
  assign or_17_out = and_33_out | or_18_out;  // OR_Gate or_17, 5 bits wide
  assign or_18_out = and_34_out | or_19_out;  // OR_Gate or_18, 5 bits wide
  assign or_19_out = and_35_out | or_20_out;  // OR_Gate or_19, 5 bits wide
  assign or_20_out = and_36_out | or_21_out;  // OR_Gate or_20, 5 bits wide
  assign or_21_out = and_37_out | or_22_out;  // OR_Gate or_21, 5 bits wide
  assign or_22_out = and_38_out | or_23_out;  // OR_Gate or_22, 5 bits wide
  assign or_23_out = and_39_out | or_24_out;  // OR_Gate or_23, 5 bits wide
  assign or_24_out = and_40_out | or_25_out;  // OR_Gate or_24, 5 bits wide
  assign or_25_out = and_41_out | or_26_out;  // OR_Gate or_25, 5 bits wide
  assign or_26_out = and_42_out | or_27_out;  // OR_Gate or_26, 5 bits wide
  assign or_27_out = and_43_out | or_28_out;  // OR_Gate or_27, 5 bits wide
  assign or_28_out = and_44_out | or_29_out;  // OR_Gate or_28, 5 bits wide
  assign or_29_out = and_45_out | or_30_out;  // OR_Gate or_29, 5 bits wide
  assign or_30_out = and_46_out | or_31_out;  // OR_Gate or_30, 5 bits wide
  assign or_31_out = and_47_out | or_32_out;  // OR_Gate or_31, 5 bits wide
  assign or_32_out = and_48_out | or_33_out;  // OR_Gate or_32, 5 bits wide
  assign or_33_out = and_49_out | {5{1'b0}};  // OR_Gate or_33, 5 bits wide

  // Notes on the sheet:
  //   Decode (D) stage.
  //   where control path values for an instruction are created in the
  //   ALU Decoder
  //   This circuit determines which ALU control code is required for the
  //   current instruction. This component lives inside the Control Unit,
  //   Given the ALUOp code output by the Main Decoder and the instruction's
  //   Funct value, the ALU Decoder determines which ALUControl value
  //   should be passed into the ALU during this instruction's execution.
  //   andi
  //   and
  //   ori
  //   or
  //   nor
  //   xori
  //   xor
  //   Exists purely for the nor instruction
  //   00000 - A & B
  //   00001 - A | B
  //   00010 - A ^ B
  //   00110 - A + B
  //   01000 - A - B
  //   01010 - A * B
  //   01100 - A / B
  //   01110 - slt Q, A, B
  //   01111 - sltu Q, A, B
  //   10000 - mfhi
  //   10001 - mthi
  //   10010 - mflo
  //   10011 - mtlo
  //   ALUOp Codes:
  //   0000 - add
  //   0001 - addu
  //   0010 - subu
  //   0011 - slt
  //   0100 - sltu
  //   0101 - and
  //   0110 - or
  //   0111 - xor
  //   00011 - A<<B (logical)
  //   00100 - A >> B (logical)
  //   00101 - A >> B (arith.)
  //   00111 - A + B (unsigned)
  //   01001 - A - B (unsigned)
  //   01011 - A * B (unsigned)
  //   01101 - A / B (unsigned)
  //   1XXX - Look at value of Funct
  //   ALUControl Codes:
  //   00000 - A & B
  //   00001 - A | B
  //   00010 - A ^ B
  //   00110 - A + B
  //   01000 - A - B
  //   01010 - A * B
  //   01100 - A / B
  //   10000 - mfhi 
  //   10001 - mthi
  //   10010 - mflo
  //   10011 - mtlo
  //   00011 - B << A (logical)
  //   00100 - B >> A (logical)
  //   00101 - B >> A (arith.)
  //   00111 - A + B (unsigned)
  //   01001 - A - B (unsigned)
  //   01011 - A * B (unsigned)
  //   01101 - A / B (unsigned)
  //   01110 - slt Q, A, B
  //   01111 - sltu Q, A, B
endmodule

module ALU (
  input  [4:0] ALUControl,
  input  [31:0] A,
  input  [31:0] B,
  input  NOT_ALUOutput,
  input  CLK,
  input  Reset,
  output [31:0] Q
);

  wire adder_1_cout, and_3_out, and_5_out, and_7_out, and_9_out, and_11_out, and_13_out, and_15_out,
       and_17_out, and_19_out, and_21_out, and_23_out, and_26_out, and_30_out, and_33_out, and_35_out,
       and_37_out, and_38_out, and_39_out, and_41_out, and_43_out, and_45_out, comparator_1_lt,
       comparator_2_lt, or_14_out, or_16_out, or_19_out, or_23_out, or_24_out, subtractor_1_bout;
  wire [31:0] adder_1_out, adder_2_out, and_1_out, and_2_out, and_4_out, and_6_out, and_8_out, and_10_out,
       and_12_out, and_14_out, and_16_out, and_18_out, and_20_out, and_22_out, and_24_out, and_25_out,
       and_27_out, and_28_out, and_29_out, and_31_out, and_32_out, and_34_out, and_36_out, and_40_out,
       and_42_out, and_44_out, bit_extender_1_out, bit_extender_2_out, bit_extender_3_out,
       bit_extender_4_out, bit_extender_5_out, bit_extender_6_out, bit_extender_7_out, bit_extender_8_out,
       bit_extender_9_out, bit_extender_10_out, bit_extender_11_out, bit_extender_12_out,
       bit_extender_13_out, bit_extender_14_out, bit_extender_15_out, bit_extender_16_out,
       bit_extender_17_out, bit_extender_18_out, bit_extender_19_out, bit_extender_20_out,
       bit_extender_21_out, divider_1_out, divider_1_rem, divider_2_out, divider_2_rem, HI_q, LO_q,
       multiplexer_2_out, multiplexer_3_out, multiplier_1_cout, multiplier_1_out, multiplier_2_cout,
       multiplier_2_out, not_1_out, or_1_out, or_2_out, or_3_out, or_4_out, or_5_out, or_6_out, or_7_out,
       or_8_out, or_9_out, or_10_out, or_11_out, or_12_out, or_13_out, or_15_out, or_17_out, or_18_out,
       or_20_out, or_21_out, or_22_out, or_25_out, or_26_out, or_27_out, or_28_out, shifter_1_out,
       shifter_2_out, shifter_3_out, subtractor_1_out, subtractor_2_out, xor_1_out, xor_2_out;

  Multiplexer #(.width(32)) multiplexer_1 (.in0(or_1_out), .in1(xor_1_out), .out(Q), .sel(NOT_ALUOutput));
  assign xor_1_out = or_1_out ^ {32{1'b1}};  // XOR_Gate xor_1, 32 bits wide
  assign and_1_out = A & B;  // AND_Gate and_1, 32 bits wide
  assign or_1_out = or_3_out | and_2_out;  // OR_Gate or_1, 32 bits wide
  assign and_2_out = and_1_out & bit_extender_1_out;  // AND_Gate and_2, 32 bits wide
  and and_3 (and_3_out, ~ALUControl[4], ~ALUControl[3], ~ALUControl[2], ~ALUControl[1], ~ALUControl[0]);  // AND_Gate
  assign bit_extender_1_out = {{31{and_3_out}}, and_3_out};  // Bit_Extender bit_extender_1
  assign or_2_out = A | B;  // OR_Gate or_2, 32 bits wide
  assign or_3_out = or_4_out | and_4_out;  // OR_Gate or_3, 32 bits wide
  assign and_4_out = or_2_out & bit_extender_2_out;  // AND_Gate and_4, 32 bits wide
  and and_5 (and_5_out, ~ALUControl[4], ~ALUControl[3], ~ALUControl[2], ~ALUControl[1], ALUControl[0]);  // AND_Gate
  assign bit_extender_2_out = {{31{and_5_out}}, and_5_out};  // Bit_Extender bit_extender_2
  assign xor_2_out = A ^ B;  // XOR_Gate xor_2, 32 bits wide
  assign or_4_out = or_5_out | and_6_out;  // OR_Gate or_4, 32 bits wide
  assign and_6_out = xor_2_out & bit_extender_3_out;  // AND_Gate and_6, 32 bits wide
  and and_7 (and_7_out, ~ALUControl[4], ~ALUControl[3], ~ALUControl[2], ALUControl[1], ~ALUControl[0]);  // AND_Gate
  assign bit_extender_3_out = {{31{and_7_out}}, and_7_out};  // Bit_Extender bit_extender_3
  Shifter #(.width(32)) shifter_1 (.in(B), .\dist (A[4:0]), .out(shifter_1_out));
  assign or_5_out = or_6_out | and_8_out;  // OR_Gate or_5, 32 bits wide
  assign and_8_out = shifter_1_out & bit_extender_4_out;  // AND_Gate and_8, 32 bits wide
  and and_9 (and_9_out, ~ALUControl[4], ~ALUControl[3], ~ALUControl[2], ALUControl[1], ALUControl[0]);  // AND_Gate
  assign bit_extender_4_out = {{31{and_9_out}}, and_9_out};  // Bit_Extender bit_extender_4
  assign or_6_out = or_7_out | and_10_out;  // OR_Gate or_6, 32 bits wide
  Shifter #(.shift("lr"), .width(32)) shifter_2 (.in(B), .\dist (A[4:0]), .out(shifter_2_out));
  assign and_10_out = shifter_2_out & bit_extender_5_out;  // AND_Gate and_10, 32 bits wide
  and and_11 (and_11_out, ~ALUControl[4], ~ALUControl[3], ALUControl[2], ~ALUControl[1], ~ALUControl[0]);  // AND_Gate
  assign bit_extender_5_out = {{31{and_11_out}}, and_11_out};  // Bit_Extender bit_extender_5
  Shifter #(.shift("ar"), .width(32)) shifter_3 (.in(B), .\dist (A[4:0]), .out(shifter_3_out));
  assign or_7_out = or_8_out | and_12_out;  // OR_Gate or_7, 32 bits wide
  assign and_12_out = shifter_3_out & bit_extender_6_out;  // AND_Gate and_12, 32 bits wide
  and and_13 (and_13_out, ~ALUControl[4], ~ALUControl[3], ALUControl[2], ~ALUControl[1], ALUControl[0]);  // AND_Gate
  assign bit_extender_6_out = {{31{and_13_out}}, and_13_out};  // Bit_Extender bit_extender_6
  Adder #(.width(32)) adder_1 (.a(A), .b(B), .out(adder_1_out), .cout(adder_1_cout));  // open: cin
  assign or_8_out = or_9_out | and_14_out;  // OR_Gate or_8, 32 bits wide
  assign and_14_out = adder_1_out & bit_extender_7_out;  // AND_Gate and_14, 32 bits wide
  and and_15 (and_15_out, ~ALUControl[4], ~ALUControl[3], ALUControl[2], ALUControl[1], ~ALUControl[0]);  // AND_Gate
  assign bit_extender_7_out = {{31{and_15_out}}, and_15_out};  // Bit_Extender bit_extender_7
  Adder #(.width(32)) adder_2 (.a(A), .b(B), .out(adder_2_out));  // open: cin, cout
  assign or_9_out = or_10_out | and_16_out;  // OR_Gate or_9, 32 bits wide
  assign and_16_out = adder_2_out & bit_extender_8_out;  // AND_Gate and_16, 32 bits wide
  and and_17 (and_17_out, ~ALUControl[4], ~ALUControl[3], ALUControl[2], ALUControl[1], ALUControl[0]);  // AND_Gate
  assign bit_extender_8_out = {{31{and_17_out}}, and_17_out};  // Bit_Extender bit_extender_8
  Subtractor #(.width(32)) subtractor_1 (.a(A), .b(B), .out(subtractor_1_out), .bout(subtractor_1_bout));  // open: bin
  assign or_10_out = or_11_out | and_18_out;  // OR_Gate or_10, 32 bits wide
  assign and_18_out = subtractor_1_out & bit_extender_9_out;  // AND_Gate and_18, 32 bits wide
  and and_19 (and_19_out, ~ALUControl[4], ALUControl[3], ~ALUControl[2], ~ALUControl[1], ~ALUControl[0]);  // AND_Gate
  assign bit_extender_9_out = {{31{and_19_out}}, and_19_out};  // Bit_Extender bit_extender_9
  Subtractor #(.width(32)) subtractor_2 (.a(A), .b(B), .out(subtractor_2_out));  // open: bin, bout
  assign or_11_out = or_21_out | and_20_out;  // OR_Gate or_11, 32 bits wide
  assign and_20_out = subtractor_2_out & bit_extender_10_out;  // AND_Gate and_20, 32 bits wide
  and and_21 (and_21_out, ~ALUControl[4], ALUControl[3], ~ALUControl[2], ~ALUControl[1], ALUControl[0]);  // AND_Gate
  assign bit_extender_10_out = {{31{and_21_out}}, and_21_out};  // Bit_Extender bit_extender_10
  Multiplier #(.mode("twosComplement"), .width(32)) multiplier_1 (
    .a(A), .b(B), .out(multiplier_1_out), .cout(multiplier_1_cout));  // open: cin
  assign and_22_out = multiplier_1_cout & bit_extender_11_out;  // AND_Gate and_22, 32 bits wide
  and and_23 (and_23_out, ~ALUControl[4], ALUControl[3], ~ALUControl[2], ALUControl[1], ~ALUControl[0]);  // AND_Gate
  assign and_24_out = multiplier_1_out & bit_extender_11_out;  // AND_Gate and_24, 32 bits wide
  assign bit_extender_11_out = {{31{and_23_out}}, and_23_out};  // Bit_Extender bit_extender_11
  Multiplier #(.width(32)) multiplier_2 (.a(A), .b(B), .out(multiplier_2_out), .cout(multiplier_2_cout));  // open: cin
  assign and_25_out = multiplier_2_cout & bit_extender_12_out;  // AND_Gate and_25, 32 bits wide
  assign or_12_out = and_25_out | and_24_out;  // OR_Gate or_12, 32 bits wide
  and and_26 (and_26_out, ~ALUControl[4], ALUControl[3], ~ALUControl[2], ALUControl[1], ALUControl[0]);  // AND_Gate
  assign and_27_out = multiplier_2_out & bit_extender_12_out;  // AND_Gate and_27, 32 bits wide
  assign or_13_out = and_27_out | and_22_out;  // OR_Gate or_13, 32 bits wide
  assign bit_extender_12_out = {{31{and_26_out}}, and_26_out};  // Bit_Extender bit_extender_12
  or or_14 (or_14_out, and_26_out, and_23_out);
  Divider #(.mode("twosComplement"), .width(32)) divider_1 (
    .a(A), .b(B), .out(divider_1_out), .rem(divider_1_rem));  // open: upper
  assign and_28_out = divider_1_rem & bit_extender_13_out;  // AND_Gate and_28, 32 bits wide
  assign or_15_out = and_28_out | or_12_out;  // OR_Gate or_15, 32 bits wide
  assign and_29_out = divider_1_out & bit_extender_13_out;  // AND_Gate and_29, 32 bits wide
  and and_30 (and_30_out, ~ALUControl[4], ALUControl[3], ALUControl[2], ~ALUControl[1], ~ALUControl[0]);  // AND_Gate
  assign bit_extender_13_out = {{31{and_30_out}}, and_30_out};  // Bit_Extender bit_extender_13
  or or_16 (or_16_out, and_30_out, or_14_out);
  assign or_17_out = and_29_out | or_13_out;  // OR_Gate or_17, 32 bits wide
  Divider #(.width(32)) divider_2 (.a(A), .b(B), .out(divider_2_out), .rem(divider_2_rem));  // open: upper
  assign and_31_out = divider_2_rem & bit_extender_14_out;  // AND_Gate and_31, 32 bits wide
  assign or_18_out = and_31_out | or_15_out;  // OR_Gate or_18, 32 bits wide
  assign and_32_out = divider_2_out & bit_extender_14_out;  // AND_Gate and_32, 32 bits wide
  and and_33 (and_33_out, ~ALUControl[4], ALUControl[3], ALUControl[2], ~ALUControl[1], ALUControl[0]);  // AND_Gate
  assign bit_extender_14_out = {{31{and_33_out}}, and_33_out};  // Bit_Extender bit_extender_14
  or or_19 (or_19_out, and_33_out, or_16_out);
  assign or_20_out = and_32_out | or_17_out;  // OR_Gate or_20, 32 bits wide
  Comparator #(.width(32)) comparator_1 (.a(A), .b(B), .lt(comparator_1_lt));  // open: gt, eq
  assign or_21_out = or_22_out | and_34_out;  // OR_Gate or_21, 32 bits wide
  assign and_34_out = bit_extender_15_out & bit_extender_16_out;  // AND_Gate and_34, 32 bits wide
  assign bit_extender_15_out = {{31{1'b0}}, comparator_1_lt};  // Bit_Extender bit_extender_15
  and and_35 (and_35_out, ~ALUControl[4], ALUControl[3], ALUControl[2], ALUControl[1], ~ALUControl[0]);  // AND_Gate
  assign bit_extender_16_out = {{31{and_35_out}}, and_35_out};  // Bit_Extender bit_extender_16
  Comparator #(.mode("unsigned"), .width(32)) comparator_2 (.a(A), .b(B), .lt(comparator_2_lt));  // open: gt, eq
  assign or_22_out = or_25_out | and_36_out;  // OR_Gate or_22, 32 bits wide
  assign bit_extender_17_out = {{31{1'b0}}, comparator_2_lt};  // Bit_Extender bit_extender_17
  assign and_36_out = bit_extender_17_out & bit_extender_18_out;  // AND_Gate and_36, 32 bits wide
  and and_37 (and_37_out, ~ALUControl[4], ALUControl[3], ALUControl[2], ALUControl[1], ALUControl[0]);  // AND_Gate
  assign bit_extender_18_out = {{31{and_37_out}}, and_37_out};  // Bit_Extender bit_extender_18
  Multiplexer #(.width(32)) multiplexer_2 (.in0(A), .in1(or_18_out), .out(multiplexer_2_out), .sel(or_19_out));
  Multiplexer #(.width(32)) multiplexer_3 (.in0(A), .in1(or_20_out), .out(multiplexer_3_out), .sel(or_19_out));
  and and_38 (and_38_out, ALUControl[4], ~ALUControl[3], ~ALUControl[2], ~ALUControl[1], ALUControl[0]);  // AND_Gate
  or or_23 (or_23_out, or_19_out, and_38_out);
  and and_39 (and_39_out, ALUControl[4], ~ALUControl[3], ~ALUControl[2], ALUControl[1], ALUControl[0]);  // AND_Gate
  or or_24 (or_24_out, or_19_out, and_39_out);
  Register #(.trigger("falling"), .width(32)) HI (
    .D(multiplexer_2_out), .en(or_23_out), .clk(CLK), .Q(HI_q), .clr(Reset));
  Register #(.trigger("falling"), .width(32)) LO (
    .D(multiplexer_3_out), .en(or_24_out), .clk(CLK), .Q(LO_q), .clr(Reset));
  assign or_25_out = or_26_out | and_40_out;  // OR_Gate or_25, 32 bits wide
  assign and_40_out = HI_q & bit_extender_19_out;  // AND_Gate and_40, 32 bits wide
  and and_41 (and_41_out, ALUControl[4], ~ALUControl[3], ~ALUControl[2], ~ALUControl[1], ~ALUControl[0]);  // AND_Gate
  assign or_26_out = or_28_out | and_42_out;  // OR_Gate or_26, 32 bits wide
  assign bit_extender_19_out = {{31{and_41_out}}, and_41_out};  // Bit_Extender bit_extender_19
  assign and_42_out = LO_q & bit_extender_20_out;  // AND_Gate and_42, 32 bits wide
  and and_43 (and_43_out, ALUControl[4], ~ALUControl[3], ~ALUControl[2], ALUControl[1], ~ALUControl[0]);  // AND_Gate
  assign bit_extender_20_out = {{31{and_43_out}}, and_43_out};  // Bit_Extender bit_extender_20
  assign or_27_out = A | B;  // OR_Gate or_27, 32 bits wide
  assign or_28_out = {32{1'b0}} | and_44_out;  // OR_Gate or_28, 32 bits wide
  assign and_44_out = not_1_out & bit_extender_21_out;  // AND_Gate and_44, 32 bits wide
  assign not_1_out = ~or_27_out;  // NOT_Gate not_1, 32 bits wide
  and and_45 (and_45_out, ALUControl[4], ~ALUControl[3], ALUControl[2], ~ALUControl[1], ALUControl[0]);  // AND_Gate
  assign bit_extender_21_out = {{31{and_45_out}}, and_45_out};  // Bit_Extender bit_extender_21

  // Notes on the sheet:
  //   the result, Q.
  //   Arithmetic Logic Unit (ALU)
  //   of the processor. Supporting a wide range of operations, 
  //   the ALU is critical to making a processor be "general-purpose."
  //   Given a control (or "OP") code and two inputs (A and B), the ALU
  //   performs the operation specified by the control code and returns
  //   This circuit performs arithmetic operations in the Execute (E) stage
  //   For specific MIPS instructions, there exists an input flag (NOT_ALUOutput)
  //   for performing a binary NOT operation on the output of the ALU (Q).
  //   00000 - A & B
  //   00001 - A | B
  //   ALUControl Codes:
  //   00000 - A & B
  //   00001 - A | B
  //   00010 - A ^ B
  //   00110 - A + B
  //   01000 - A - B
  //   01010 - A * B
  //   01100 - A / B
  //   00011 - B << A (logical)
  //   00100 - B >> A (logical)
  //   00101 - B >> A (arith.)
  //   00111 - A + B (unsigned)
  //   01001 - A - B (unsigned)
  //   01011 - A * B (unsigned)
  //   01101 - A / B (unsigned)
  //   01110 - slt Q, A, B
  //   01111 - sltu Q, A, B
  //   00010 - A ^ B
  //   10000 - mfhi 
  //   10001 - mthi
  //   10010 - mflo
  //   10011 - mtlo
  //   10100 - ~(A | B)
  //   10101 - N/A
  //   1011x - N/A
  //   11xxx - N/A
  //   00011 - B << A (sll)
  //   00100 - B >> A (srl)
  //   00101 - B >> A (sra)
  //   00110 - A + B
  //   Overflow
  //   00111 - A + B (addu)
  //   01000 - A - B
  //   Overflow
  //   01001 - A - B (subu)
  //   01010 - A * B
  //   01011 - A * B (unsigned)
  //   01100 - A / B
  //   01101 - A / B (unsigned)
  //   01110 - slt Q, A, B
  //   01111 - sltu Q, A, B
  //   10001 - mthi
  //   10011 - mtlo
  //   10000 - mfhi 
  //   10010 - mflo
  //   10101 - ~(A | B)
endmodule

module RegisterFile (
  input  [4:0] Address1,
  input  [4:0] Address2,
  input  WriteEnable3,
  input  [4:0] Address3,
  input  [31:0] WriteData3,
  input  CLK,
  input  Reset,
  output [31:0] RegisterData1,
  output [31:0] RegisterData2,
  output [31:0] a0
);

  wire demultiplexer_1_out0, demultiplexer_1_out1, demultiplexer_1_out2, demultiplexer_1_out3,
       demultiplexer_2_out0, demultiplexer_2_out1, demultiplexer_2_out2, demultiplexer_2_out3,
       demultiplexer_2_out4, demultiplexer_2_out5, demultiplexer_2_out6, demultiplexer_2_out7,
       demultiplexer_3_out0, demultiplexer_3_out1, demultiplexer_3_out2, demultiplexer_3_out3,
       demultiplexer_3_out4, demultiplexer_3_out5, demultiplexer_3_out6, demultiplexer_3_out7,
       demultiplexer_4_out0, demultiplexer_4_out1, demultiplexer_4_out2, demultiplexer_4_out3,
       demultiplexer_4_out4, demultiplexer_4_out5, demultiplexer_4_out6, demultiplexer_4_out7,
       demultiplexer_5_out0, demultiplexer_5_out1, demultiplexer_5_out2, demultiplexer_5_out3,
       demultiplexer_5_out4, demultiplexer_5_out5, demultiplexer_5_out6, demultiplexer_5_out7, or_1_out,
       or_2_out, or_3_out;
  wire [31:0] multiplexer_2_out, multiplexer_3_out, multiplexer_4_out, r00_0_q, r0a_t2_q, r0b_t3_q, r0c_t4_q,
       r0d_t5_q, r0e_t6_q, r0f_t7_q, r01_at_q, r1a_k0_q, r1b_k1_q, r1c_gp_q, r1d_sp_q, r1e_fp_q, r1f_ra_q,
       r02_v0_q, r03_v1_q, r05_a1_q, r06_a2_q, r07_a3_q, r08_t0_q, r09_t1_q, r10_s0_q, r11_s1_q, r12_s2_q,
       r13_s3_q, r14_s4_q, r15_s5_q, r16_s6_q, r17_s7_q, r18_t8_q, r19_t9_q;

  Demultiplexer #(.select(2)) demultiplexer_1 (
    .out0(demultiplexer_1_out0), .out1(demultiplexer_1_out1), .out2(demultiplexer_1_out2),
    .out3(demultiplexer_1_out3), .in(WriteEnable3), .sel(Address3[4:3]));
  Demultiplexer #(.select(3)) demultiplexer_2 (
    .out0(demultiplexer_2_out0), .out1(demultiplexer_2_out1), .out2(demultiplexer_2_out2),
    .out3(demultiplexer_2_out3), .out4(demultiplexer_2_out4), .out5(demultiplexer_2_out5),
    .out6(demultiplexer_2_out6), .out7(demultiplexer_2_out7), .in(demultiplexer_1_out0), .sel(Address3[2:0]));
  Register #(.trigger("falling"), .width(32)) r00_0 (
    .D({32{1'b0}}), .en(demultiplexer_2_out0), .clk(CLK), .Q(r00_0_q), .clr(Reset));
  Register #(.trigger("falling"), .width(32)) r01_at (
    .D(WriteData3), .en(demultiplexer_2_out1), .clk(CLK), .Q(r01_at_q), .clr(Reset));
  Register #(.trigger("falling"), .width(32)) r02_v0 (
    .D(WriteData3), .en(demultiplexer_2_out2), .clk(CLK), .Q(r02_v0_q), .clr(Reset));
  Register #(.trigger("falling"), .width(32)) r03_v1 (
    .D(WriteData3), .en(demultiplexer_2_out3), .clk(CLK), .Q(r03_v1_q), .clr(Reset));
  Register #(.trigger("falling"), .width(32)) r04_a0 (
    .D(WriteData3), .en(demultiplexer_2_out4), .clk(CLK), .Q(a0), .clr(Reset));
  Register #(.trigger("falling"), .width(32)) r05_a1 (
    .D(WriteData3), .en(demultiplexer_2_out5), .clk(CLK), .Q(r05_a1_q), .clr(Reset));
  Register #(.trigger("falling"), .width(32)) r06_a2 (
    .D(WriteData3), .en(demultiplexer_2_out6), .clk(CLK), .Q(r06_a2_q), .clr(Reset));
  Register #(.trigger("falling"), .width(32)) r07_a3 (
    .D(WriteData3), .en(demultiplexer_2_out7), .clk(CLK), .Q(r07_a3_q), .clr(Reset));
  Demultiplexer #(.select(3)) demultiplexer_3 (
    .out0(demultiplexer_3_out0), .out1(demultiplexer_3_out1), .out2(demultiplexer_3_out2),
    .out3(demultiplexer_3_out3), .out4(demultiplexer_3_out4), .out5(demultiplexer_3_out5),
    .out6(demultiplexer_3_out6), .out7(demultiplexer_3_out7), .in(demultiplexer_1_out1), .sel(Address3[2:0]));
  Register #(.trigger("falling"), .width(32)) r08_t0 (
    .D(WriteData3), .en(demultiplexer_3_out0), .clk(CLK), .Q(r08_t0_q), .clr(Reset));
  Register #(.trigger("falling"), .width(32)) r09_t1 (
    .D(WriteData3), .en(demultiplexer_3_out1), .clk(CLK), .Q(r09_t1_q), .clr(Reset));
  Register #(.trigger("falling"), .width(32)) r0a_t2 (
    .D(WriteData3), .en(demultiplexer_3_out2), .clk(CLK), .Q(r0a_t2_q), .clr(Reset));
  Register #(.trigger("falling"), .width(32)) r0b_t3 (
    .D(WriteData3), .en(demultiplexer_3_out3), .clk(CLK), .Q(r0b_t3_q), .clr(Reset));
  Register #(.trigger("falling"), .width(32)) r0c_t4 (
    .D(WriteData3), .en(demultiplexer_3_out4), .clk(CLK), .Q(r0c_t4_q), .clr(Reset));
  Register #(.trigger("falling"), .width(32)) r0d_t5 (
    .D(WriteData3), .en(demultiplexer_3_out5), .clk(CLK), .Q(r0d_t5_q), .clr(Reset));
  Register #(.trigger("falling"), .width(32)) r0e_t6 (
    .D(WriteData3), .en(demultiplexer_3_out6), .clk(CLK), .Q(r0e_t6_q), .clr(Reset));
  Register #(.trigger("falling"), .width(32)) r0f_t7 (
    .D(WriteData3), .en(demultiplexer_3_out7), .clk(CLK), .Q(r0f_t7_q), .clr(Reset));
  Demultiplexer #(.select(3)) demultiplexer_4 (
    .out0(demultiplexer_4_out0), .out1(demultiplexer_4_out1), .out2(demultiplexer_4_out2),
    .out3(demultiplexer_4_out3), .out4(demultiplexer_4_out4), .out5(demultiplexer_4_out5),
    .out6(demultiplexer_4_out6), .out7(demultiplexer_4_out7), .in(demultiplexer_1_out2), .sel(Address3[2:0]));
  Register #(.trigger("falling"), .width(32)) r10_s0 (
    .D(WriteData3), .en(demultiplexer_4_out0), .clk(CLK), .Q(r10_s0_q), .clr(Reset));
  Register #(.trigger("falling"), .width(32)) r11_s1 (
    .D(WriteData3), .en(demultiplexer_4_out1), .clk(CLK), .Q(r11_s1_q), .clr(Reset));
  Register #(.trigger("falling"), .width(32)) r12_s2 (
    .D(WriteData3), .en(demultiplexer_4_out2), .clk(CLK), .Q(r12_s2_q), .clr(Reset));
  Register #(.trigger("falling"), .width(32)) r13_s3 (
    .D(WriteData3), .en(demultiplexer_4_out3), .clk(CLK), .Q(r13_s3_q), .clr(Reset));
  Register #(.trigger("falling"), .width(32)) r14_s4 (
    .D(WriteData3), .en(demultiplexer_4_out4), .clk(CLK), .Q(r14_s4_q), .clr(Reset));
  Register #(.trigger("falling"), .width(32)) r15_s5 (
    .D(WriteData3), .en(demultiplexer_4_out5), .clk(CLK), .Q(r15_s5_q), .clr(Reset));
  Register #(.trigger("falling"), .width(32)) r16_s6 (
    .D(WriteData3), .en(demultiplexer_4_out6), .clk(CLK), .Q(r16_s6_q), .clr(Reset));
  Register #(.trigger("falling"), .width(32)) r17_s7 (
    .D(WriteData3), .en(demultiplexer_4_out7), .clk(CLK), .Q(r17_s7_q), .clr(Reset));
  Demultiplexer #(.select(3)) demultiplexer_5 (
    .out0(demultiplexer_5_out0), .out1(demultiplexer_5_out1), .out2(demultiplexer_5_out2),
    .out3(demultiplexer_5_out3), .out4(demultiplexer_5_out4), .out5(demultiplexer_5_out5),
    .out6(demultiplexer_5_out6), .out7(demultiplexer_5_out7), .in(demultiplexer_1_out3), .sel(Address3[2:0]));
  Multiplexer #(.select(5), .width(32)) multiplexer_1 (
    .in0(r00_0_q), .in1(r01_at_q), .in2(r02_v0_q), .in3(r03_v1_q), .in4(a0), .in5(r05_a1_q), .in6(r06_a2_q),
    .in7(r07_a3_q), .in8(r08_t0_q), .in9(r09_t1_q), .in10(r0a_t2_q), .in11(r0b_t3_q), .in12(r0c_t4_q),
    .in13(r0d_t5_q), .in14(r0e_t6_q), .in15(r0f_t7_q), .in16(r10_s0_q), .in17(r11_s1_q), .in18(r12_s2_q),
    .in19(r13_s3_q), .in20(r14_s4_q), .in21(r15_s5_q), .in22(r16_s6_q), .in23(r17_s7_q), .in24(r18_t8_q),
    .in25(r19_t9_q), .in26(r1a_k0_q), .in27(r1b_k1_q), .in28(r1c_gp_q), .in29(r1d_sp_q), .in30(r1e_fp_q),
    .in31(r1f_ra_q), .out(RegisterData1), .sel(Address1));
  Register #(.trigger("falling"), .width(32)) r18_t8 (
    .D(WriteData3), .en(demultiplexer_5_out0), .clk(CLK), .Q(r18_t8_q), .clr(Reset));
  Register #(.trigger("falling"), .width(32)) r19_t9 (
    .D(WriteData3), .en(demultiplexer_5_out1), .clk(CLK), .Q(r19_t9_q), .clr(Reset));
  Register #(.trigger("falling"), .width(32)) r1a_k0 (
    .D(WriteData3), .en(demultiplexer_5_out2), .clk(CLK), .Q(r1a_k0_q), .clr(Reset));
  Register #(.trigger("falling"), .width(32)) r1b_k1 (
    .D(WriteData3), .en(demultiplexer_5_out3), .clk(CLK), .Q(r1b_k1_q), .clr(Reset));
  Register #(.trigger("falling"), .width(32)) r1c_gp (
    .D(multiplexer_2_out), .en(or_1_out), .clk(CLK), .Q(r1c_gp_q));  // open: clr
  Multiplexer #(.width(32)) multiplexer_2 (.in0(WriteData3), .in1(32'h7f000000), .out(multiplexer_2_out), .sel(Reset));
  or or_1 (or_1_out, demultiplexer_5_out4, Reset);
  Register #(.trigger("falling"), .width(32)) r1d_sp (
    .D(multiplexer_3_out), .en(or_2_out), .clk(CLK), .Q(r1d_sp_q));  // open: clr
  Multiplexer #(.width(32)) multiplexer_3 (.in0(WriteData3), .in1(32'h80000000), .out(multiplexer_3_out), .sel(Reset));
  or or_2 (or_2_out, demultiplexer_5_out5, Reset);
  Register #(.trigger("falling"), .width(32)) r1e_fp (
    .D(multiplexer_4_out), .en(or_3_out), .clk(CLK), .Q(r1e_fp_q));  // open: clr
  Multiplexer #(.width(32)) multiplexer_4 (.in0(WriteData3), .in1(32'h80000000), .out(multiplexer_4_out), .sel(Reset));
  or or_3 (or_3_out, demultiplexer_5_out6, Reset);
  Register #(.trigger("falling"), .width(32)) r1f_ra (
    .D(WriteData3), .en(demultiplexer_5_out7), .clk(CLK), .Q(r1f_ra_q), .clr(Reset));
  Multiplexer #(.select(5), .width(32)) multiplexer_5 (
    .in0(r00_0_q), .in1(r01_at_q), .in2(r02_v0_q), .in3(r03_v1_q), .in4(a0), .in5(r05_a1_q), .in6(r06_a2_q),
    .in7(r07_a3_q), .in8(r08_t0_q), .in9(r09_t1_q), .in10(r0a_t2_q), .in11(r0b_t3_q), .in12(r0c_t4_q),
    .in13(r0d_t5_q), .in14(r0e_t6_q), .in15(r0f_t7_q), .in16(r10_s0_q), .in17(r11_s1_q), .in18(r12_s2_q),
    .in19(r13_s3_q), .in20(r14_s4_q), .in21(r15_s5_q), .in22(r16_s6_q), .in23(r17_s7_q), .in24(r18_t8_q),
    .in25(r19_t9_q), .in26(r1a_k0_q), .in27(r1b_k1_q), .in28(r1c_gp_q), .in29(r1d_sp_q), .in30(r1e_fp_q),
    .in31(r1f_ra_q), .out(RegisterData2), .sel(Address2));

  // Notes on the sheet:
  //   Register File
  //   the Writeback (W) stage.
  //   Registers addressed 0-31
  //   32-bit registers
  //   Write on falling clock edge,
  //   Read is async
  //   edge of CLK if WriteEnable3 is HIGH.
  //   Register File
  //   This circuit holds all general-purpose registers of the processor.
  //   Placed within the Decode (D) stage, allows register reads inside
  //   the Decode (D) stage while synchronously writing values from
  //   Given two register addresses (Address1 & Address2), the Register File
  //   outputs their respective registers' values (RegisterData1 & RegisterData2).
  //   Additionally, the Register File overwrites the contents of the register of another
  //   given address (Address3) with a new value (WriteData3) on the FALLING
  //   Write Functionality
  //   Register Addresses:
  //   00000 - $0
  //   00001 - $at
  //   00010 - $v0
  //   00011 - $v1
  //   00100 - $a0
  //   00101 - $a1
  //   00110 - $a2
  //   00111 - $a3
  //   01000 - $t0
  //   01001 - $t1
  //   01010 - $t2
  //   01011 - $t3
  //   01100 - $t4
  //   01101 - $t5
  //   01110 - $t6
  //   01111 - $t7
  //   10000 - $s0
  //   10001 - $s1
  //   10010 - $s2
  //   10011 - $s3
  //   10100 - $s4
  //   10101 - $s5
  //   10110 - $s6
  //   10111 - $s7
  //   11000 - $t8
  //   11001 - $t9
  //   11010 - $k0
  //   11011 - $k1
  //   11100 - $gp
  //   11101 - $sp
  //   11110 - $fp
  //   11111 - $t7
  //   Breakout used for printing character stored in $a0
  //   Reading Functionality
  //   0
  //   32
  //   Outputs of Registers
endmodule
module InstructionMemory (
  input  [31:0] Address,
  output InvalidAddressFlag,
  output [31:0] Instruction
);

  wire Kernel_InvalidAddressFlag, subtractor_1_bout, subtractor_2_bout, Text_InvalidAddressFlag;
  wire [1:0] not_2_out;
  wire [31:0] Kernel_Instruction, subtractor_1_out, subtractor_2_out, Text_Instruction;

  Subtractor #(.width(32)) subtractor_1 (
    .a(Address), .b(32'h400000), .out(subtractor_1_out), .bout(subtractor_1_bout));  // open: bin
  Subtractor #(.width(32)) subtractor_2 (
    .a(Address), .b(32'h80000000), .out(subtractor_2_out), .bout(subtractor_2_bout));  // open: bin
  or or_1 (Text_InvalidAddressFlag, subtractor_1_bout, subtractor_1_out[31], subtractor_1_out[30], subtractor_1_out[29], subtractor_1_out[28], subtractor_1_out[27], subtractor_1_out[26], subtractor_1_out[1], subtractor_1_out[0]);
  ROM #(.addrWidth(24), .dataWidth(32)) user_text_section (
    .addr(subtractor_1_out[25:2]),
    .data({Text_Instruction[7:0], Text_Instruction[15:8], Text_Instruction[23:16], Text_Instruction[31:24]}));
  ROM #(.addrWidth(24), .dataWidth(32)) kernel_text_section (
    .addr(subtractor_2_out[25:2]),
    .data({Kernel_Instruction[7:0], Kernel_Instruction[15:8], Kernel_Instruction[23:16], Kernel_Instruction[31:24]}));
  or or_2 (Kernel_InvalidAddressFlag, subtractor_2_bout, subtractor_2_out[31], subtractor_2_out[30], subtractor_2_out[29], subtractor_2_out[28], subtractor_2_out[27], subtractor_2_out[26], subtractor_2_out[1], subtractor_2_out[0]);
  not not_1 (not_2_out[1], Kernel_InvalidAddressFlag);
  not not_2 (not_2_out[0], Text_InvalidAddressFlag);
  Multiplexer #(.select(2), .width(32)) multiplexer_1 (
    .in0({32{1'b0}}), .in1(Text_Instruction), .in2(Kernel_Instruction), .out(Instruction), .sel(not_2_out));  // open: in3
  and and_1 (InvalidAddressFlag, Text_InvalidAddressFlag, Kernel_InvalidAddressFlag);

  // Notes on the sheet:
  //   This circuit contains the ROM modules which store instructions for
  //   the currently loaded program.  Rather than just storing the ".text"
  //   section of the currently loaded program, this circuit also stores
  //   the processor's kernel which handles syscalls.
  //   The first region of memory stored by this circuit is the program instruction
  //   memory (or the ".text" region). This spans from address 0x00400000 to
  //   0x043fffff. In other words, this region is 64MB starting at address 0x00400000.
  //   Additionally, this circuit stores the kernel's instruction memory
  //   (or the ".ktext" region). This spans from address 0x80000000 to 0x803fffff.
  //   In other words, this region is 64MB starting at address 0x80000000.
  //   Given a word-aligned address (Address), this circuit outputs
  //   the 32-bit instruction (Instruction) stored at the given address.
  //   If Address is not word-aligned or not within a region of memory
  //   stored by this circuit, a nop instruction is output and the
  //   InvalidAddressFlag output is set HIGH.
  //   Kernel Instr. Memory Range:
  //   0x8000 0000 - 0x803f ffff
  //   Instruction Memory Range:
  //   0x0040 0000 - 0x043f ffff
  //   Instruction Memory
  //   contents of user_text_section (hex, n*v repeats v):
  //   600100c 0 a000224 25d0e003 c000000 0 f4ffbd23 800bfaf 400beaf 400be23 fcffc0af 4000224 10043c
  //   7d048424 25d0e003 c000000 0 25100000 8800100c 0 b300100c 0 de00100c 0 901100c 0 3401100c 0 5f01100c
  //   0 8a01100c 0 b501100c 0 e001100c 0 b02100c 0 3602100c 0 6102100c 0 8c02100c 0 b702100c 0 fcffd08f 0
  //   0 700001e 0 10043c be048424 4000224 25d0e003 c000000 0 400df8f 0 de8f 0 c00bd23 800e003 0 f4ffbd23
  //   800bfaf 400beaf 400be23 fcffc4af 38008510 0 4000224 2520e000 25d0e003 c000000 0 b000224 a000424
  //   25d0e003 c000000 0 1000830 c8ac 10043c 8f048424 25d0e003 c000000 0 10043c 96048424 25d0e003 c000000
  //   0 1000224 100c422 25d0e003 c000000 0 4000224 10043c a4048424 25d0e003 c000000 0 1000224 fcffc48f 0
  //   25d0e003 c000000 0 10043c b0048424 4000224 25d0e003 c000000 0 1000224 2520a000 25d0e003 c000000 0
  //   b000224 a000424 25d0e003 c000000 0 400df8f 0 fcffc48f 0 0 de8f 0 c00bd23 800e003 0 f8ffbd23 400bfaf
  //   beaf be23 25308000 10113c 4003126 10133c 14007326 10153c 2400b526 1624 10173c f726 f78e 0 1200d712 0
  //   308e 0 4003122 728e 0 4007322 a58e 0 400b522 20201202 10073c 6002e724 4000100c 0 100d622 98001008 0
  //   400df8f 0 de8f 0 800bd23 2520c000 800e003 0 f8ffbd23 400bfaf beaf be23 25308000 10113c 38003126
  //   10133c 44007326 10153c 5000b526 1624 10173c 3400f726 f78e 0 1200d712 0 308e 0 4003122 728e 0 4007322
  //   a58e 0 400b522 211000 10073c 7b02e724 4000100c 0 100d622 c3001008 0 400df8f 0 de8f 0 800bd23
  //   2520c000 800e003 0 f8ffbd23 400bfaf beaf be23 25308000 10113c 60003126 10133c 6c007326 10153c
  //   7800b526 1624 10173c 5c00f726 f78e 0 1200d712 0 308e 0 4003122 728e 0 4007322 a58e 0 400b522 201000
  //   10073c 9402e724 4000100c 0 100d622 ee001008 0 400df8f 0 de8f 0 800bd23 2520c000 800e003 0 f8ffbd23
  //   400bfaf beaf be23 25308000 10113c 88003126 10133c 94007326 10153c a000b526 1624 10173c 8400f726 f78e
  //   0 1200d712 0 308e 0 4003122 728e 0 4007322 a58e 0 400b522 c0271000 10073c ad02e724 4000100c 0
  //   100d622 19011008 0 400df8f 0 de8f 0 800bd23 2520c000 800e003 0 f8ffbd23 400bfaf beaf be23 25308000
  //   10113c b0003126 10133c bc007326 10153c c800b526 1624 10173c ac00f726 f78e 0 1200d712 0 308e 0
  //   4003122 728e 0 4007322 a58e 0 400b522 2211000 10073c c702e724 4000100c 0 100d622 44011008 0 400df8f
  //   0 de8f 0 800bd23 2520c000 800e003 0 f8ffbd23 400bfaf beaf be23 25308000 10113c d8003126 10133c
  //   e4007326 10153c f000b526 1624 10173c d400f726 f78e 0 1200d712 0 308e 0 4003122 728e 0 4007322 a58e 0
  //   400b522 2201000 10073c e002e724 4000100c 0 100d622 6f011008 0 400df8f 0 de8f 0 800bd23 2520c000
  //   800e003 0 f8ffbd23 400bfaf beaf be23 25308000 10113c 13126 10133c c017326 10153c 1801b526 1624
  //   10173c fc00f726 f78e 0 1200d712 0 308e 0 4003122 728e 0 4007322 a58e 0 400b522 c2271000 10073c
  //   f902e724 4000100c 0 100d622 9a011008 0 400df8f 0 de8f 0 800bd23 2520c000 800e003 0 f8ffbd23 400bfaf
  //   beaf be23 25308000 10113c 28013126 10133c 34017326 10153c 4001b526 1624 10173c 2401f726 f78e 0
  //   1200d712 0 308e 0 4003122 728e 0 4007322 a58e 0 400b522 3211000 10073c 1303e724 4000100c 0 100d622
  //   c5011008 0 400df8f 0 de8f 0 800bd23 2520c000 800e003 0 f8ffbd23 400bfaf beaf be23 25308000 10113c
  //   50013126 10133c 5c017326 10153c 6801b526 1624 10173c 4c01f726 f78e 0 1200d712 0 308e 0 4003122 728e
  //   0 4007322 a58e 0 400b522 3201000 10073c 2c03e724 4000100c 0 100d622 f0011008 0 400df8f 0 de8f 0
  //   800bd23 2520c000 800e003 0 f8ffbd23 400bfaf beaf be23 25308000 10113c 78013126 10133c 84017326
  //   10153c 9001b526 1624 10173c 7401f726 f78e 0 1200d712 0 308e 0 4003122 728e 0 4007322 a58e 0 400b522
  //   c3271000 10073c 4503e724 4000100c 0 100d622 1b021008 0 400df8f 0 de8f 0 800bd23 2520c000 800e003 0
  //   f8ffbd23 400bfaf beaf be23 25308000 10113c a0013126 10133c b0017326 10153c c001b526 1624 10173c
  //   9c01f726 f78e 0 1200d712 0 308e 0 4003122 728e 0 4007322 a58e 0 400b522 4205002 10073c 6003e724
  //   4000100c 0 100d622 46021008 0 400df8f 0 de8f 0 800bd23 2520c000 800e003 0 f8ffbd23 400bfaf beaf be23
  //   25308000 10113c d4013126 10133c e4017326 10153c f401b526 1624 10173c d001f726 f78e 0 1200d712 0 308e
  //   0 4003122 728e 0 4007322 a58e 0 400b522 6205002 10073c 7d03e724 4000100c 0 100d622 7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
  //   contents of kernel_text_section (hex, n*v repeats v):
  //   a001b24 2005b14 0 50 ecffbd27 1000bfaf c00abaf 800aaaf 400a9af a8af 1000824 5004814 0 2e00000c 0
  //   20000008 0 4000824 5004814 0 5b00000c 0 20000008 0 b000824 5004814 0 6d00000c 0 20000008 0 0
  //   1000bb8f 0 c00ab8f 0 800aa8f 0 400a98f 0 a88f 0 1400bd23 25f84003 8006003 0 f0ffbd27 c00bfaf a000824
  //   2a488000 6008014 0 30008420 6d00000c 0 56000008 0 200801c 0 23200400 a00aa23 10040a1 f008010 0
  //   2000015 1b008800 d000700 12200000 0 0 10580000 0 0 30006b21 4ba1 ffff4a21 3e000008 0 4002011 0
  //   2d000b24 4ba1 ffff4a21 1004421 5b00000c 0 c00bf8f 0 1000bd23 800e003 0 25408000 fcffbd27 bfaf 481 0
  //   6008010 0 6d00000c 0 1000825 f8ff0010 0 bf8f 0 a0af 400bd27 800e003 0 54 800e003
  //   Register Addresses:
  //   00000 - $0
  //   00001 - $at
  //   00010 - $v0
  //   00011 - $v1
  //   00100 - $a0
  //   00101 - $a1
  //   00110 - $a2
  //   00111 - $a3
  //   01000 - $t0
  //   01001 - $t1
  //   01010 - $t2
  //   01011 - $t3
  //   01100 - $t4
  //   01101 - $t5
  //   01110 - $t6
  //   01111 - $t7
  //   <<=======
  //   <<=======
  //   <<=======
  //   <<=======
  //   10000 - $s0
  //   10001 - $s1
  //   10010 - $s2
  //   10011 - $s3
  //   10100 - $s4
  //   10101 - $s5
  //   10110 - $s6
  //   10111 - $s7
  //   11000 - $t8
  //   11001 - $t9
  //   11010 - $k0
  //   11011 - $k1
  //   11100 - $gp
  //   11101 - $sp
  //   11110 - $fp
  //   11111 - $t7
  //   LOAD "text.hex" FILE HERE!
  //   RIGHT CLICK RAM:
  //   Load Image > Choose "text.hex"
  //   THIS IS KERNEL TEXT SECTION
  //   DO NOT MODIFY
  //   OP: 20; exit
  //   OP: 21; print char
endmodule

module DataPathRegister_F_D (
  input  [31:0] Instruction_F,
  input  [31:0] PCPlus4_F,
  input  CLK,
  input  Reset,
  output [31:0] Instruction_D,
  output [31:0] PCPlus4_D
);

  Register #(.width(32)) register_1 (.D(Instruction_F), .clk(CLK), .Q(Instruction_D), .clr(Reset));  // open: en
  Register #(.width(32)) register_2 (.D(PCPlus4_F), .clk(CLK), .Q(PCPlus4_D), .clr(Reset));  // open: en
endmodule

module DataPathRegister_D_E (
  input  [31:0] RegData1_D,
  input  [31:0] RegData2_D,
  input  [4:0] rt_D,
  input  [4:0] rd_D,
  input  [4:0] shamt_D,
  input  [31:0] SignImm_D,
  input  [31:0] PCPlus4_D,
  input  CLK,
  input  Reset,
  output [31:0] RegData1_E,
  output [31:0] RegData2_E,
  output [4:0] rt_E,
  output [4:0] rd_E,
  output [4:0] shamt_E,
  output [31:0] SignImm_E,
  output [31:0] PCPlus4_E
);

  Register #(.width(32)) register_1 (.D(RegData1_D), .clk(CLK), .Q(RegData1_E), .clr(Reset));  // open: en
  Register #(.width(32)) register_2 (.D(RegData2_D), .clk(CLK), .Q(RegData2_E), .clr(Reset));  // open: en
  Register #(.width(5)) register_3 (.D(rt_D), .clk(CLK), .Q(rt_E), .clr(Reset));  // open: en
  Register #(.width(5)) register_4 (.D(rd_D), .clk(CLK), .Q(rd_E), .clr(Reset));  // open: en
  Register #(.width(5)) register_5 (.D(shamt_D), .clk(CLK), .Q(shamt_E), .clr(Reset));  // open: en
  Register #(.width(32)) register_6 (.D(SignImm_D), .clk(CLK), .Q(SignImm_E), .clr(Reset));  // open: en
  Register #(.width(32)) register_7 (.D(PCPlus4_D), .clk(CLK), .Q(PCPlus4_E), .clr(Reset));  // open: en
endmodule

module DataPathRegister_E_M (
  input  [31:0] ALUOut_E,
  input  [31:0] UpperImm_E,
  input  [31:0] MemWriteData_E,
  input  [4:0] WriteReg_E,
  input  [31:0] PCPlus4_E,
  input  CLK,
  input  Reset,
  output [31:0] ALUOut_M,
  output [31:0] UpperImm_M,
  output [31:0] MemWriteData_M,
  output [4:0] WriteReg_M,
  output [31:0] PCPlus4_M
);

  Register #(.width(32)) register_1 (.D(ALUOut_E), .clk(CLK), .Q(ALUOut_M), .clr(Reset));  // open: en
  Register #(.width(32)) register_2 (.D(UpperImm_E), .clk(CLK), .Q(UpperImm_M), .clr(Reset));  // open: en
  Register #(.width(32)) register_3 (.D(MemWriteData_E), .clk(CLK), .Q(MemWriteData_M), .clr(Reset));  // open: en
  Register #(.width(5)) register_4 (.D(WriteReg_E), .clk(CLK), .Q(WriteReg_M), .clr(Reset));  // open: en
  Register #(.width(32)) register_5 (.D(PCPlus4_E), .clk(CLK), .Q(PCPlus4_M), .clr(Reset));  // open: en
endmodule

module DataPathRegister_M_W (
  input  [31:0] ALUOut_M,
  input  [31:0] UpperImm_M,
  input  [31:0] MemReadData_M,
  input  [31:0] PCPlus4_M,
  input  [4:0] WriteReg_M,
  input  CLK,
  input  Reset,
  output [31:0] ALUOut_W,
  output [31:0] UpperImm_W,
  output [31:0] MemReadData_W,
  output [31:0] PCPlus4_W,
  output [4:0] WriteReg_W
);

  Register #(.width(32)) register_1 (.D(ALUOut_M), .clk(CLK), .Q(ALUOut_W), .clr(Reset));  // open: en
  Register #(.width(32)) register_2 (.D(UpperImm_M), .clk(CLK), .Q(UpperImm_W), .clr(Reset));  // open: en
  Register #(.width(32)) register_3 (.D(MemReadData_M), .clk(CLK), .Q(MemReadData_W), .clr(Reset));  // open: en
  Register #(.width(32)) register_4 (.D(PCPlus4_M), .clk(CLK), .Q(PCPlus4_W), .clr(Reset));  // open: en
  Register #(.width(5)) register_5 (.D(WriteReg_M), .clk(CLK), .Q(WriteReg_W), .clr(Reset));  // open: en
endmodule

module ControlPathRegister_D_E (
  input  RegWrite_D,
  input  [1:0] RegWriteDataSrc_D,
  input  [3:0] MemOp_D,
  input  [4:0] ALUControl_D,
  input  NOT_ALUOut_D,
  input  ALUSrcA_D,
  input  [1:0] ALUSrcB_D,
  input  WriteRegSrc_D,
  input  CLK,
  input  Reset,
  output RegWrite_E,
  output [1:0] RegWriteDataSrc_E,
  output [3:0] MemOp_E,
  output [4:0] ALUControl_E,
  output NOT_ALUOut_E,
  output ALUSrcA_E,
  output [1:0] ALUSrcB_E,
  output WriteRegSrc_E
);

  Register #(.width(1)) register_1 (.D(RegWrite_D), .clk(CLK), .Q(RegWrite_E), .clr(Reset));  // open: en
  Register #(.width(2)) register_2 (.D(RegWriteDataSrc_D), .clk(CLK), .Q(RegWriteDataSrc_E), .clr(Reset));  // open: en
  Register #(.width(4)) register_3 (.D(MemOp_D), .clk(CLK), .Q(MemOp_E), .clr(Reset));  // open: en
  Register #(.width(5)) register_4 (.D(ALUControl_D), .clk(CLK), .Q(ALUControl_E), .clr(Reset));  // open: en
  Register #(.width(1)) register_5 (.D(NOT_ALUOut_D), .clk(CLK), .Q(NOT_ALUOut_E), .clr(Reset));  // open: en
  Register #(.width(1)) register_6 (.D(ALUSrcA_D), .clk(CLK), .Q(ALUSrcA_E), .clr(Reset));  // open: en
  Register #(.width(2)) register_7 (.D(ALUSrcB_D), .clk(CLK), .Q(ALUSrcB_E), .clr(Reset));  // open: en
  Register #(.width(1)) register_8 (.D(WriteRegSrc_D), .clk(CLK), .Q(WriteRegSrc_E), .clr(Reset));  // open: en
endmodule

module ControlPathRegister_E_M (
  input  RegWrite_E,
  input  [1:0] RegWriteDataSrc_E,
  input  [3:0] MemOp_E,
  input  CLK,
  input  Reset,
  output RegWrite_M,
  output [1:0] RegWriteDataSrc_M,
  output [3:0] MemOp_M
);

  Register #(.width(1)) register_1 (.D(RegWrite_E), .clk(CLK), .Q(RegWrite_M), .clr(Reset));  // open: en
  Register #(.width(2)) register_2 (.D(RegWriteDataSrc_E), .clk(CLK), .Q(RegWriteDataSrc_M), .clr(Reset));  // open: en
  Register #(.width(4)) register_3 (.D(MemOp_E), .clk(CLK), .Q(MemOp_M), .clr(Reset));  // open: en
endmodule

module ControlPathRegister_M_W (
  input  RegWrite_M,
  input  [1:0] RegWriteDataSrc_M,
  input  CLK,
  input  Reset,
  output RegWrite_W,
  output [1:0] RegWriteDataSrc_W
);

  Register #(.width(1)) register_1 (.D(RegWrite_M), .clk(CLK), .Q(RegWrite_W), .clr(Reset));  // open: en
  Register #(.width(2)) register_2 (.D(RegWriteDataSrc_M), .clk(CLK), .Q(RegWriteDataSrc_W), .clr(Reset));  // open: en
endmodule

module HazardShield_D (
  input  [31:0] Instruction_D,
  input  RegWrite_E,
  input  IsMemOp_E,
  input  [4:0] WriteReg_E,
  input  [31:0] RegWriteData_E,
  input  RegWrite_M,
  input  [4:0] WriteReg_M,
  input  [31:0] RegWriteData_M,
  output [4:0] rs_D,
  output [4:0] rt_D,
  output OverrideRegData1_D,
  output [31:0] RegData1_D,
  output OverrideRegData2_D,
  output [31:0] RegData2_D
);

  wire and_1_out, and_2_out, and_3_out, and_4_out, and_5_out, comparator_1_eq, comparator_2_eq,
       comparator_3_eq, comparator_4_eq;

  and and_1 (and_1_out, RegWrite_E, ~IsMemOp_E);  // AND_Gate
  // Probe on Instruction_D[20:16]
  // Probe on Instruction_D[25:21]
  Comparator #(.width(5)) comparator_1 (
    .a(Instruction_D[25:21]), .b(WriteReg_E), .eq(comparator_1_eq));  // open: gt, lt
  and and_2 (and_2_out, comparator_1_eq, and_1_out);
  Comparator #(.width(5)) comparator_2 (
    .a(Instruction_D[20:16]), .b(WriteReg_E), .eq(comparator_2_eq));  // open: gt, lt
  and and_3 (and_3_out, comparator_2_eq, and_1_out);
  and and_4 (and_4_out, RegWrite_M, comparator_3_eq);
  Comparator #(.width(5)) comparator_3 (
    .a(Instruction_D[25:21]), .b(WriteReg_M), .eq(comparator_3_eq));  // open: gt, lt
  and and_5 (and_5_out, RegWrite_M, comparator_4_eq);
  Comparator #(.width(5)) comparator_4 (
    .a(Instruction_D[20:16]), .b(WriteReg_M), .eq(comparator_4_eq));  // open: gt, lt
  Multiplexer #(.width(32)) multiplexer_1 (
    .in0(RegWriteData_E), .in1(RegWriteData_M), .out(RegData1_D), .sel(and_4_out));
  Multiplexer #(.width(32)) multiplexer_2 (
    .in0(RegWriteData_E), .in1(RegWriteData_M), .out(RegData2_D), .sel(and_5_out));
  or or_1 (OverrideRegData1_D, and_2_out, and_4_out);
  or or_2 (OverrideRegData2_D, and_3_out, and_5_out);

  assign rs_D = Instruction_D[25:21];
  assign rt_D = Instruction_D[20:16];

  // Notes on the sheet:
  //   Ways a register value can be modified:
  //   - ALU Operation
  //   - Load upper immediate (lui)
  //   - Load from memory
  //   - Update $ra with jal
  //   <-- Requires value to have been read from memory (this data cannot be forwarded from E to D stage)
endmodule

module HazardShield_E (
  input  [4:0] rs_D,
  input  [4:0] rt_D,
  input  RegWrite_M,
  input  [4:0] WriteReg_M,
  input  [31:0] RegWriteData_M,
  input  CLK,
  input  Reset,
  output OverrideRegData1_E,
  output [31:0] RegData1_E,
  output OverrideRegData2_E,
  output [31:0] RegData2_E
);

  wire comparator_1_eq, comparator_2_eq;
  wire [4:0] register_1_q, register_2_q;

  Register #(.width(5)) register_1 (.D(rs_D), .clk(CLK), .Q(register_1_q), .clr(Reset));  // open: en
  Register #(.width(5)) register_2 (.D(rt_D), .clk(CLK), .Q(register_2_q), .clr(Reset));  // open: en
  Comparator #(.width(5)) comparator_1 (.a(register_1_q), .b(WriteReg_M), .eq(comparator_1_eq));  // open: gt, lt
  Comparator #(.width(5)) comparator_2 (.a(register_2_q), .b(WriteReg_M), .eq(comparator_2_eq));  // open: gt, lt
  and and_1 (OverrideRegData1_E, RegWrite_M, comparator_1_eq);
  and and_2 (OverrideRegData2_E, RegWrite_M, comparator_2_eq);

  assign RegData1_E = RegWriteData_M;
  assign RegData2_E = RegWriteData_M;

  // Notes on the sheet:
  //   rs_E
  //   rt_E
endmodule

module MM_Preprocessor (
  input  [3:0] MemOp,
  input  [31:0] Address,
  input  [31:0] InputData,
  input  CLK,
  output [4:0] Data_MemOpANDAlign,
  output [23:0] Data_RAMAddr,
  output [6:0] Data_Enables,
  output [31:0] Data_DataIn,
  output Data_InvalidAddressFlag,
  output [4:0] Stack_MemOpANDAlign,
  output [23:0] Stack_RAMAddr,
  output [6:0] Stack_Enables,
  output [31:0] Stack_DataIn,
  output Stack_InvalidAddressFlag
);

  wire and_1_out, and_2_out, and_3_out, and_4_out, and_5_out, and_6_out, nand_1_out, nand_2_out, nand_3_out,
       nand_4_out, nand_5_out, nand_6_out;
  wire [1:0] xor_1_out, xor_2_out;
  wire [1:1] not_2_out;
  wire [3:0] multiplexer_3_out;
  wire [5:1] multiplexer_2_out;
  wire [6:0] bit_extender_1_out, bit_extender_2_out;
  wire [31:0] shifter_1_out, shifter_2_out, shifter_3_out, shifter_4_out;
  wire [31:26] subtractor_1_out, subtractor_2_out;

  Subtractor #(.width(32)) subtractor_1 (
    .a(Address), .b(32'h10000000), .out({subtractor_1_out, Data_RAMAddr, Data_MemOpANDAlign[4:3]}));  // open: bin, bout
  not not_1 (multiplexer_2_out[1], MemOp[3]);
  and and_1 (and_1_out, Data_MemOpANDAlign[4], ~MemOp[2], MemOp[1], ~MemOp[0]);  // AND_Gate
  Subtractor #(.width(32)) subtractor_2 (
    .a(Address), .b(32'h7c000000), .out({subtractor_2_out, Stack_RAMAddr, Stack_MemOpANDAlign[4:3]}));  // open: bin, bout
  nand nand_1 (nand_1_out, MemOp[2], MemOp[3]);
  and and_2 (and_2_out, Data_MemOpANDAlign[4], nand_1_out, MemOp[1], ~MemOp[0]);  // AND_Gate
  not not_2 (not_2_out[1], MemOp[3]);
  nand nand_2 (nand_2_out, MemOp[2], MemOp[3]);
  and and_3 (and_3_out, Data_MemOpANDAlign[3], nand_2_out, ~MemOp[1], MemOp[0]);  // AND_Gate
  or or_1 (Data_InvalidAddressFlag, and_1_out, and_2_out, and_3_out, subtractor_1_out[26], subtractor_1_out[27], subtractor_1_out[28], subtractor_1_out[29], subtractor_1_out[30], subtractor_1_out[31]);
  nand nand_3 (nand_3_out, MemOp[2], MemOp[3]);
  and and_4 (and_4_out, Stack_MemOpANDAlign[4], ~MemOp[2], MemOp[1], ~MemOp[0]);  // AND_Gate
  and and_5 (and_5_out, Stack_MemOpANDAlign[4], nand_3_out, MemOp[1], ~MemOp[0]);  // AND_Gate
  assign xor_1_out = 2'b11 ^ Data_MemOpANDAlign[4:3];  // XOR_Gate xor_1, 2 bits wide
  nand nand_4 (nand_4_out, MemOp[2], MemOp[3]);
  and and_6 (and_6_out, Stack_MemOpANDAlign[3], nand_4_out, ~MemOp[1], MemOp[0]);  // AND_Gate
  or or_2 (Stack_InvalidAddressFlag, and_4_out, and_5_out, and_6_out, subtractor_2_out[26], subtractor_2_out[27], subtractor_2_out[28], subtractor_2_out[29], subtractor_2_out[30], subtractor_2_out[31]);
  Shifter #(.width(32)) shifter_1 (
    .in({InputData[7:0], InputData[15:8], InputData[23:16], InputData[31:24]}), .\dist ({xor_1_out, 3'b000}),
    .out(shifter_1_out));
  Shifter #(.shift("lr"), .width(32)) shifter_2 (
    .in({InputData[7:0], InputData[15:8], InputData[23:16], InputData[31:24]}),
    .\dist ({Data_MemOpANDAlign[4:3], 3'b000}), .out(shifter_2_out));
  assign xor_2_out = 2'b11 ^ Stack_MemOpANDAlign[4:3];  // XOR_Gate xor_2, 2 bits wide
  nand nand_5 (nand_5_out, MemOp[2], MemOp[1], MemOp[0]);
  Multiplexer #(.width(32)) multiplexer_1 (
    .in0(shifter_1_out), .in1(shifter_2_out), .out(Data_DataIn), .sel(nand_5_out));
  Multiplexer #(.select(5), .width(4)) multiplexer_2 (
    .in0(4'b1000), .in1(4'b1100), .in2(4'b1111), .in3(4'b0000), .in4(4'b0000), .in5(4'b0000), .in6(4'b1000),
    .in7(4'b1111), .in8(4'b0100), .in9(4'b0000), .in10(4'b0000), .in11(4'b0000), .in12(4'b0000),
    .in13(4'b0000), .in14(4'b1100), .in15(4'b1110), .in16(4'b0010), .in17(4'b0011), .in18(4'b0000),
    .in19(4'b0000), .in20(4'b0000), .in21(4'b0000), .in22(4'b1110), .in23(4'b0011), .in24(4'b0001),
    .in25(4'b0000), .in26(4'b0000), .in27(4'b0000), .in28(4'b0000), .in29(4'b0000), .in30(4'b1111),
    .in31(4'b0001),
    .out({multiplexer_2_out[2], multiplexer_2_out[3], multiplexer_2_out[4], multiplexer_2_out[5]}),
    .sel({Data_MemOpANDAlign[4:3], MemOp[2:0]}));
  nand nand_6 (nand_6_out, MemOp[2], MemOp[1], MemOp[0]);
  Shifter #(.width(32)) shifter_3 (
    .in({InputData[7:0], InputData[15:8], InputData[23:16], InputData[31:24]}), .\dist ({xor_2_out, 3'b000}),
    .out(shifter_3_out));
  Shifter #(.shift("lr"), .width(32)) shifter_4 (
    .in({InputData[7:0], InputData[15:8], InputData[23:16], InputData[31:24]}),
    .\dist ({Stack_MemOpANDAlign[4:3], 3'b000}), .out(shifter_4_out));
  Multiplexer #(.select(5), .width(4)) multiplexer_3 (
    .in0(4'b1000), .in1(4'b1100), .in2(4'b1111), .in3(4'b0000), .in4(4'b0000), .in5(4'b0000), .in6(4'b1000),
    .in7(4'b1111), .in8(4'b0100), .in9(4'b0000), .in10(4'b0000), .in11(4'b0000), .in12(4'b0000),
    .in13(4'b0000), .in14(4'b1100), .in15(4'b1110), .in16(4'b0010), .in17(4'b0011), .in18(4'b0000),
    .in19(4'b0000), .in20(4'b0000), .in21(4'b0000), .in22(4'b1110), .in23(4'b0011), .in24(4'b0001),
    .in25(4'b0000), .in26(4'b0000), .in27(4'b0000), .in28(4'b0000), .in29(4'b0000), .in30(4'b1111),
    .in31(4'b0001), .out(multiplexer_3_out), .sel({Stack_MemOpANDAlign[4:3], MemOp[2:0]}));
  Multiplexer #(.width(32)) multiplexer_4 (
    .in0(shifter_3_out), .in1(shifter_4_out), .out(Stack_DataIn), .sel(nand_6_out));
  assign Data_Enables = {CLK, multiplexer_2_out, MemOp[3]} & ~bit_extender_1_out;  // AND_Gate and_7, 7 bits wide
  assign bit_extender_1_out = {{6{Data_InvalidAddressFlag}}, Data_InvalidAddressFlag};  // Bit_Extender bit_extender_1
  assign bit_extender_2_out = {{6{Stack_InvalidAddressFlag}}, Stack_InvalidAddressFlag};  // Bit_Extender bit_extender_2
  assign Stack_Enables = {CLK, multiplexer_3_out[0], multiplexer_3_out[1], multiplexer_3_out[2], multiplexer_3_out[3], not_2_out[1], MemOp[3]} & ~bit_extender_2_out;  // AND_Gate and_8, 7 bits wide

  assign Data_MemOpANDAlign[2:0] = MemOp[2:0];
  assign Stack_MemOpANDAlign[2:0] = MemOp[2:0];

  // Notes on the sheet:
  //   Flip byte order (BE -> LE) -->
  //   Flip byte order (BE -> LE) -->
  //   InvalidAddressFlag:
  //   0 - Valid Address
  //   <-- Invalid alignment
  //   flags
  //   1. Address out of range
  //   InvalidAddressFlag:
  //   1 - Invalid Address for any of the following reasons:
  //   <-- Invalid alignment
  //   flags
  //   0 - Valid Address
  //   1. Address out of range
  //   unless is swr instruction.
  //   2. Attempting to write/read a non-word aligned word
  //   3. Attempting to write/read a non-halfword aligned halfword
  //   1 - Invalid Address for any of the following reasons:
  //   Shifts logical right by Address % 4 bytes
  //   unless is swr instruction.
  //   2. Attempting to write/read a non-word aligned word
  //   3. Attempting to write/read a non-halfword aligned halfword
  //   Shifts logical right by Address % 4 bytes
  //   <- Write Enable
  //   <- Read Enable
  //   <-- MUX Maps memory operations to
  //   enable flags on Logisim RAM module.
  //   <- Write Enable
  //   <- Read Enable
  //   <-- MUX Maps memory operations to
  //   enable flags on Logisim RAM module.
endmodule

module MM_Postprocessor (
  input  [4:0] Data_MemOpANDAlignment,
  input  [31:0] Data_RAMOut,
  input  Data_InvalidAddressFlag,
  input  [4:0] Stack_MemOpANDAlignment,
  input  [31:0] Stack_RAMOut,
  input  Stack_InvalidAddressFlag,
  output AdES_AddressErrorException,
  output [31:0] DataOut
);

  wire priority_encoder_1_out;
  wire [1:0] not_1_out, xor_1_out, xor_2_out;
  wire [7:0] multiplexer_1_out, multiplexer_3_out;
  wire [15:0] multiplexer_2_out, multiplexer_4_out;
  wire [31:0] bit_extender_1_out, bit_extender_2_out, bit_extender_3_out, bit_extender_4_out,
       bit_extender_5_out, bit_extender_6_out, bit_extender_7_out, bit_extender_8_out, multiplexer_5_out,
       multiplexer_6_out, multiplexer_7_out, multiplexer_8_out, multiplexer_9_out, multiplexer_10_out,
       multiplexer_11_out, multiplexer_12_out, multiplexer_13_out, multiplexer_14_out, multiplexer_15_out,
       shifter_1_out, shifter_2_out, shifter_3_out, shifter_4_out;

  Multiplexer #(.select(2), .width(8)) multiplexer_1 (
    .in0(Data_RAMOut[31:24]), .in1(Data_RAMOut[23:16]), .in2(Data_RAMOut[15:8]), .in3(Data_RAMOut[7:0]),
    .out(multiplexer_1_out), .sel(Data_MemOpANDAlignment[4:3]));
  Multiplexer #(.select(2), .width(16)) multiplexer_2 (
    .in0({Data_RAMOut[7:0], Data_RAMOut[15:8]}), .in2({Data_RAMOut[23:16], Data_RAMOut[31:24]}),
    .out(multiplexer_2_out), .sel(Data_MemOpANDAlignment[4:3]));  // open: in1, in3
  Multiplexer #(.select(2), .width(8)) multiplexer_3 (
    .in0(Stack_RAMOut[31:24]), .in1(Stack_RAMOut[23:16]), .in2(Stack_RAMOut[15:8]), .in3(Stack_RAMOut[7:0]),
    .out(multiplexer_3_out), .sel(Stack_MemOpANDAlignment[4:3]));
  Multiplexer #(.select(2), .width(16)) multiplexer_4 (
    .in0({Stack_RAMOut[7:0], Stack_RAMOut[15:8]}), .in2({Stack_RAMOut[23:16], Stack_RAMOut[31:24]}),
    .out(multiplexer_4_out), .sel(Stack_MemOpANDAlignment[4:3]));  // open: in1, in3
  assign xor_1_out = 2'b11 ^ Stack_MemOpANDAlignment[4:3];  // XOR_Gate xor_1, 2 bits wide
  assign bit_extender_1_out = {{24{multiplexer_1_out[7]}}, multiplexer_1_out};  // Bit_Extender bit_extender_1
  assign bit_extender_2_out = {{24{1'b0}}, multiplexer_1_out};  // Bit_Extender bit_extender_2
  assign bit_extender_3_out = {{16{multiplexer_2_out[15]}}, multiplexer_2_out};  // Bit_Extender bit_extender_3
  assign bit_extender_4_out = {{16{1'b0}}, multiplexer_2_out};  // Bit_Extender bit_extender_4
  assign xor_2_out = 2'b11 ^ Data_MemOpANDAlignment[4:3];  // XOR_Gate xor_2, 2 bits wide
  assign bit_extender_5_out = {{24{multiplexer_3_out[7]}}, multiplexer_3_out};  // Bit_Extender bit_extender_5
  assign bit_extender_6_out = {{24{1'b0}}, multiplexer_3_out};  // Bit_Extender bit_extender_6
  assign bit_extender_7_out = {{16{multiplexer_4_out[15]}}, multiplexer_4_out};  // Bit_Extender bit_extender_7
  assign bit_extender_8_out = {{16{1'b0}}, multiplexer_4_out};  // Bit_Extender bit_extender_8
  Shifter #(.width(32)) shifter_1 (
    .in({Stack_RAMOut[7:0], Stack_RAMOut[15:8], Stack_RAMOut[23:16], Stack_RAMOut[31:24]}),
    .\dist ({xor_1_out, 3'b000}), .out(shifter_1_out));
  Multiplexer #(.width(32)) multiplexer_5 (
    .in0(bit_extender_1_out), .in1(bit_extender_2_out), .out(multiplexer_5_out),
    .sel(Data_MemOpANDAlignment[2]));
  Multiplexer #(.width(32)) multiplexer_6 (
    .in0(bit_extender_3_out), .in1(bit_extender_4_out), .out(multiplexer_6_out),
    .sel(Data_MemOpANDAlignment[2]));
  Shifter #(.width(32)) shifter_2 (
    .in({Data_RAMOut[7:0], Data_RAMOut[15:8], Data_RAMOut[23:16], Data_RAMOut[31:24]}),
    .\dist ({xor_2_out, 3'b000}), .out(shifter_2_out));
  Shifter #(.shift("lr"), .width(32)) shifter_3 (
    .in({Data_RAMOut[7:0], Data_RAMOut[15:8], Data_RAMOut[23:16], Data_RAMOut[31:24]}),
    .\dist ({Data_MemOpANDAlignment[4:3], 3'b000}), .out(shifter_3_out));
  Multiplexer #(.width(32)) multiplexer_7 (
    .in0(bit_extender_5_out), .in1(bit_extender_6_out), .out(multiplexer_7_out),
    .sel(Stack_MemOpANDAlignment[2]));
  Multiplexer #(.width(32)) multiplexer_8 (
    .in0(bit_extender_7_out), .in1(bit_extender_8_out), .out(multiplexer_8_out),
    .sel(Stack_MemOpANDAlignment[2]));
  Shifter #(.shift("lr"), .width(32)) shifter_4 (
    .in({Stack_RAMOut[7:0], Stack_RAMOut[15:8], Stack_RAMOut[23:16], Stack_RAMOut[31:24]}),
    .\dist ({Stack_MemOpANDAlignment[4:3], 3'b000}), .out(shifter_4_out));
  Multiplexer #(.width(32)) multiplexer_9 (
    .in0({Data_RAMOut[7:0], Data_RAMOut[15:8], Data_RAMOut[23:16], Data_RAMOut[31:24]}), .in1(shifter_2_out),
    .out(multiplexer_9_out), .sel(Data_MemOpANDAlignment[2]));
  Multiplexer #(.width(32)) multiplexer_10 (
    .in0({32{1'b0}}), .in1(shifter_3_out), .out(multiplexer_10_out), .sel(Data_MemOpANDAlignment[2]));
  Multiplexer #(.width(32)) multiplexer_11 (
    .in0({Stack_RAMOut[7:0], Stack_RAMOut[15:8], Stack_RAMOut[23:16], Stack_RAMOut[31:24]}),
    .in1(shifter_1_out), .out(multiplexer_11_out), .sel(Stack_MemOpANDAlignment[2]));
  Multiplexer #(.width(32)) multiplexer_12 (
    .in0({32{1'b0}}), .in1(shifter_4_out), .out(multiplexer_12_out), .sel(Stack_MemOpANDAlignment[2]));
  Multiplexer #(.select(2), .width(32)) multiplexer_13 (
    .in0(multiplexer_5_out), .in1(multiplexer_6_out), .in2(multiplexer_9_out), .in3(multiplexer_10_out),
    .out(multiplexer_13_out), .sel(Data_MemOpANDAlignment[1:0]));
  Multiplexer #(.select(2), .width(32)) multiplexer_14 (
    .in0(multiplexer_7_out), .in1(multiplexer_8_out), .in2(multiplexer_11_out), .in3(multiplexer_12_out),
    .out(multiplexer_14_out), .sel(Stack_MemOpANDAlignment[1:0]));
  assign not_1_out = ~{Stack_InvalidAddressFlag, Data_InvalidAddressFlag};  // NOT_Gate not_1, 2 bits wide
  Priority_Encoder #(.select(1)) priority_encoder_1 (
    .in0(not_1_out[0]), .in1(not_1_out[1]), .out(priority_encoder_1_out), .en_out(AdES_AddressErrorException));  // open: gs, en_in
  Multiplexer #(.width(32)) multiplexer_15 (
    .in0(multiplexer_13_out), .in1(multiplexer_14_out), .out(multiplexer_15_out), .sel(priority_encoder_1_out));
  Multiplexer #(.width(32)) multiplexer_16 (
    .in0(multiplexer_15_out), .in1({32{1'b0}}), .out(DataOut), .sel(AdES_AddressErrorException));

  // Notes on the sheet:
  //   lb/lbu
  //   lh/lhu
  //   lb/lbu
  //   lh/lhu
  //   lw/lwl
  //   nop/lwr
  //   lw/lwl
  //   nop/lwr
endmodule

module ClockDivider (
  input  CLK,
  input  IsSyscall_F,
  input  Reset,
  output CLK_OUT
);

  wire comparator_1_gt, not_1_out, or_1_out;
  wire [31:0] counter_1_q;

  not not_1 (not_1_out, IsSyscall_F);
  Counter #(.max('h200), .width(32)) counter_1 (
    .count(not_1_out), .Q(counter_1_q), .clk(CLK), .clr(Reset));  // open: load, D, carry, up
  or or_1 (or_1_out, Reset, IsSyscall_F);
  Comparator #(.mode("unsigned"), .width(32)) comparator_1 (
    .a(counter_1_q), .b(32'h100), .gt(comparator_1_gt));  // open: eq, lt
  Multiplexer multiplexer_1 (.in0(comparator_1_gt), .in1(CLK), .out(CLK_OUT), .sel(or_1_out));
endmodule

module KBD_Postprocessor (
  input  [6:0] Data,
  input  CM_TRUE_CLK,
  output CM_CLK,
  output Reset,
  output PS_Reset
);

  wire and_1_out, comparator_4_eq, isAutoTicking, isLowercaseR, isLowercaseT, isSpace, not_1_out, or_1_out;
  wire [7:0] counter_1_q;

  Comparator #(.mode("unsigned"), .width(7)) comparator_1 (.a(Data), .b(7'b0100000), .eq(isSpace));  // open: gt, lt
  Comparator #(.mode("unsigned"), .width(7)) comparator_2 (
    .a(Data), .b(7'b1110010), .eq(isLowercaseR));  // open: gt, lt
  Comparator #(.mode("unsigned"), .width(7)) comparator_3 (
    .a(Data), .b(7'b1110100), .eq(isLowercaseT));  // open: gt, lt
  Counter #(.ongoal("stay")) counter_1 (
    .load(isLowercaseR), .D(8'h5), .Q(counter_1_q), .up(1'b0), .clk(CM_TRUE_CLK));  // open: count, carry, clr
  Comparator #(.mode("unsigned")) comparator_4 (.a(counter_1_q), .b(8'h3), .eq(comparator_4_eq));  // open: gt, lt
  Comparator #(.mode("unsigned")) comparator_5 (.a(counter_1_q), .b({8{1'b0}}), .gt(Reset));  // open: eq, lt
  Comparator #(.mode("unsigned")) comparator_6 (.a(counter_1_q), .b(8'h4), .eq(PS_Reset));  // open: gt, lt
  not not_1 (not_1_out, isAutoTicking);
  Register #(.width(1)) register_1 (.D(not_1_out), .clk(isLowercaseT), .Q(isAutoTicking), .clr(Reset));  // open: en
  or or_1 (or_1_out, isSpace, comparator_4_eq);
  and and_1 (and_1_out, isAutoTicking, ~Reset);  // AND_Gate
  Multiplexer multiplexer_1 (.in0(or_1_out), .in1(CM_TRUE_CLK), .out(CM_CLK), .sel(and_1_out));

  // Other names for the same wires on the sheet: CLK = CM_TRUE_CLK

  // Notes on the sheet:
  //   Reset Procedure:
  //   1. "Reset" HIGH; "CM_CLK" LOW for 2 "CM_TRUE_CLK" cycles
  //   2. "Reset" HIGH; "CM_CLK" HIGH for 1 "CM_TRUE_CLK" cycle
  //   3. "Reset" HIGH; "CM_CLK" LOW for 2 "CM_TRUE_CLK" cycles
  //   <- If counter == 3, CM_CLK == HIGH
endmodule
